// Logisim project 8bit_computer.circ as structural Verilog: 1 circuit, main circuit main
module main (
);

  wire and_1_out, and_2_out, and_3_out, and_4_out, and_5_out, and_6_out, and_7_out, and_8_out, and_9_out,
       and_10_out, and_11_out, and_12_out, and_13_out, and_14_out, and_15_out, and_16_out, and_17_out,
       and_18_out, and_19_out, and_20_out, and_21_out, and_22_out, and_23_out, and_24_out, and_25_out,
       and_26_out, and_27_out, and_28_out, and_29_out, and_30_out, and_31_out, and_32_out, and_33_out,
       and_34_out, and_35_out, and_36_out, and_37_out, and_38_out, and_39_out, and_40_out, and_41_out,
       and_42_out, and_43_out, and_44_out, and_45_out, and_46_out, and_47_out, and_48_out, and_49_out,
       and_50_out, and_51_out, and_52_out, and_53_out, and_54_out, and_55_out, and_56_out, and_57_out,
       and_58_out, and_59_out, and_60_out, and_61_out, and_62_out, and_63_out, and_64_out, and_65_out,
       and_66_out, and_67_out, and_68_out, and_69_out, and_70_out, and_71_out, and_72_out, and_73_out,
       and_74_out, and_75_out, and_76_out, and_77_out, and_78_out, and_79_out, and_80_out, and_81_out,
       and_82_out, and_83_out, and_84_out, and_85_out, and_86_out, and_87_out, and_88_out, and_89_out,
       and_90_out, and_91_out, and_92_out, and_93_out, and_94_out, and_95_out, and_96_out, and_97_out,
       and_98_out, and_99_out, and_100_out, and_101_out, and_102_out, and_103_out, and_104_out, and_105_out,
       and_106_out, and_107_out, and_108_out, and_109_out, and_110_out, and_111_out, and_112_out,
       and_113_out, and_114_out, and_115_out, and_116_out, and_117_out, and_118_out, and_119_out,
       and_120_out, and_121_out, and_122_out, and_123_out, and_124_out, and_125_out, and_126_out,
       and_127_out, and_128_out, and_129_out, and_130_out, and_131_out, and_132_out, and_133_out,
       and_134_out, and_135_out, and_136_out, and_137_out, and_138_out, and_139_out, and_140_out,
       and_141_out, and_142_out, and_143_out, and_144_out, and_145_out, and_146_out, and_147_out,
       and_148_out, and_149_out, and_150_out, and_151_out, and_152_out, and_153_out, and_154_out,
       and_155_out, and_156_out, and_157_out, and_158_out, and_159_out, and_160_out, and_161_out,
       and_162_out, and_163_out, and_164_out, and_165_out, and_166_out, and_167_out, and_168_out,
       and_169_out, and_170_out, and_171_out, and_172_out, and_173_out, and_174_out, and_175_out,
       and_176_out, and_177_out, and_178_out, and_179_out, and_180_out, and_181_out, and_182_out,
       and_183_out, and_184_out, and_185_out, and_186_out, and_187_out, and_188_out, and_189_out,
       and_190_out, and_191_out, and_192_out, and_193_out, and_194_out, and_195_out, and_196_out,
       and_197_out, and_198_out, and_199_out, and_200_out, and_201_out, and_202_out, and_203_out,
       and_204_out, and_205_out, and_206_out, and_207_out, and_208_out, and_209_out, and_210_out,
       and_211_out, and_212_out, and_213_out, and_214_out, and_215_out, and_216_out, and_217_out,
       and_218_out, and_219_out, and_220_out, and_221_out, and_222_out, and_223_out, and_224_out,
       and_225_out, and_226_out, and_227_out, and_228_out, and_229_out, and_230_out, and_231_out,
       and_232_out, and_233_out, and_234_out, and_235_out, and_236_out, and_237_out, and_238_out,
       and_239_out, and_240_out, and_241_out, and_242_out, and_243_out, and_244_out, and_245_out,
       and_246_out, and_247_out, and_248_out, and_249_out, and_250_out, and_251_out, and_252_out,
       and_253_out, and_254_out, and_255_out, and_256_out, and_257_out, and_258_out, and_259_out,
       and_260_out, and_261_out, and_262_out, and_263_out, and_264_out, and_265_out, and_266_out,
       and_267_out, and_268_out, and_269_out, and_270_out, and_271_out, and_272_out, and_273_out,
       and_274_out, and_275_out, and_276_out, and_277_out, and_278_out, and_279_out, and_280_out,
       and_281_out, and_282_out, and_283_out, and_284_out, and_285_out, and_286_out, and_287_out,
       and_288_out, and_289_out, and_290_out, and_291_out, and_292_out, and_293_out, and_294_out,
       and_295_out, and_296_out, and_297_out, and_298_out, and_299_out, and_300_out, and_301_out,
       and_302_out, and_303_out, and_304_out, and_305_out, and_306_out, buffer_1_out, buffer_2_out,
       buffer_3_out, buffer_4_out, buffer_5_out, buffer_6_out, buffer_7_out, buffer_8_out, buffer_17_out,
       buffer_18_out, buffer_19_out, buffer_20_out, buffer_21_out, buffer_22_out, buffer_23_out,
       buffer_24_out, buffer_25_out, buffer_26_out, buffer_27_out, buffer_28_out, buffer_29_out,
       buffer_30_out, buffer_31_out, buffer_32_out, buffer_33_out, buffer_34_out, buffer_35_out,
       buffer_36_out, buffer_37_out, buffer_38_out, buffer_39_out, buffer_40_out, buffer_41_out,
       buffer_42_out, buffer_43_out, buffer_44_out, buffer_45_out, buffer_46_out, buffer_47_out,
       buffer_48_out, buffer_49_out, buffer_54_out, buffer_58_out, buffer_59_out, buffer_60_out,
       buffer_61_out, buffer_62_out, buffer_63_out, buffer_64_out, buffer_65_out, buffer_74_out,
       buffer_75_out, buffer_76_out, buffer_77_out, buffer_78_out, buffer_79_out, buffer_80_out,
       buffer_81_out, buffer_90_out, buffer_91_out, buffer_92_out, buffer_93_out, buffer_94_out,
       buffer_95_out, buffer_96_out, buffer_97_out, buffer_106_out, buffer_107_out, buffer_108_out,
       buffer_109_out, buffer_110_out, buffer_111_out, buffer_112_out, buffer_113_out, buffer_122_out,
       buffer_123_out, buffer_124_out, buffer_125_out, buffer_126_out, buffer_127_out, buffer_128_out,
       buffer_129_out, buffer_138_out, buffer_139_out, buffer_140_out, buffer_141_out, buffer_142_out,
       buffer_143_out, buffer_144_out, buffer_145_out, buffer_154_out, buffer_155_out, buffer_156_out,
       buffer_157_out, buffer_158_out, buffer_159_out, buffer_160_out, buffer_161_out, buffer_170_out,
       buffer_171_out, buffer_172_out, buffer_173_out, buffer_174_out, buffer_175_out, buffer_176_out,
       buffer_177_out, buffer_186_out, buffer_187_out, buffer_188_out, buffer_189_out, buffer_190_out,
       buffer_191_out, buffer_192_out, buffer_193_out, button_1_out, button_2_out, button_3_out,
       button_4_out, button_5_out, button_6_out, button_7_out, button_8_out, button_9_out, button_10_out,
       button_11_out, button_12_out, button_13_out, button_14_out, button_15_out, button_16_out,
       button_17_out, button_18_out, button_19_out, button_20_out, button_21_out, button_22_out,
       button_23_out, clock_1_out, clock_2_out, digital_oscilloscope_1_p1, digital_oscilloscope_1_p2,
       digital_oscilloscope_2_p1, digital_oscilloscope_2_p2, dipswitch_1_sw1, dipswitch_1_sw2,
       dipswitch_1_sw3, dipswitch_1_sw4, dipswitch_1_sw5, dipswitch_1_sw6, dipswitch_1_sw7, dipswitch_1_sw8,
       dipswitch_2_sw8, dipswitch_3_sw1, dipswitch_4_sw1, dipswitch_5_sw1, dipswitch_6_sw1, dipswitch_6_sw4,
       dipswitch_7_sw4, dipswitch_8_sw4, dipswitch_9_sw4, dipswitch_10_sw4, dipswitch_11_sw4,
       dipswitch_12_sw4, dipswitch_13_sw4, dipswitch_14_sw1, dipswitch_14_sw8, dipswitch_16_sw8, j_k_ff_1_q,
       j_k_ff_2_q, j_k_ff_3_q, j_k_ff_4_q, j_k_ff_5_q, j_k_ff_6_q, j_k_ff_7_q, j_k_ff_8_q, j_k_ff_9_q,
       j_k_ff_10_q, j_k_ff_11_q, j_k_ff_12_q, j_k_ff_13_q, j_k_ff_14_q, j_k_ff_15_q, j_k_ff_16_q, not_1_out,
       not_2_out, not_3_out, not_4_out, not_5_out, not_6_out, not_7_out, not_9_out, not_10_out, not_11_out,
       not_12_out, not_13_out, not_14_out, not_15_out, or_1_out, or_2_out, or_3_out, or_4_out, or_5_out,
       or_6_out, or_7_out, or_8_out, or_9_out, or_10_out, or_11_out, or_12_out, or_13_out, or_14_out,
       or_15_out, or_16_out, s_r_ff_1_q, s_r_ff_2_q, s_r_ff_3_q, s_r_ff_4_q, s_r_ff_5_q, s_r_ff_6_q,
       s_r_ff_7_q, s_r_ff_8_q, s_r_ff_9_q, s_r_ff_10_q, s_r_ff_11_q, s_r_ff_12_q, s_r_ff_13_q, s_r_ff_14_q,
       s_r_ff_15_q, s_r_ff_16_q, s_r_ff_17_q, s_r_ff_18_q, s_r_ff_19_q, s_r_ff_20_q, s_r_ff_21_q,
       s_r_ff_22_q, s_r_ff_23_q, s_r_ff_24_q, s_r_ff_25_q, s_r_ff_26_q, s_r_ff_27_q, s_r_ff_28_q,
       s_r_ff_29_q, s_r_ff_30_q, s_r_ff_31_q, s_r_ff_32_q, s_r_ff_33_q, s_r_ff_34_q, s_r_ff_35_q,
       s_r_ff_36_q, s_r_ff_37_q, s_r_ff_38_q, s_r_ff_39_q, s_r_ff_40_q, s_r_ff_41_q, s_r_ff_42_q,
       s_r_ff_43_q, s_r_ff_44_q, s_r_ff_45_q, s_r_ff_46_q, s_r_ff_47_q, s_r_ff_48_q, s_r_ff_49_q,
       s_r_ff_50_q, s_r_ff_51_q, s_r_ff_52_q, s_r_ff_53_q, s_r_ff_54_q, s_r_ff_55_q, s_r_ff_56_q,
       s_r_ff_57_q, s_r_ff_58_q, s_r_ff_59_q, s_r_ff_60_q, s_r_ff_61_q, s_r_ff_62_q, s_r_ff_63_q,
       s_r_ff_64_q, s_r_ff_65_q, s_r_ff_66_q, s_r_ff_67_q, s_r_ff_68_q, s_r_ff_69_q, s_r_ff_70_q,
       s_r_ff_71_q, s_r_ff_72_q, s_r_ff_73_q, s_r_ff_74_q, s_r_ff_75_q, s_r_ff_76_q, s_r_ff_77_q,
       s_r_ff_78_q, s_r_ff_79_q, s_r_ff_80_q, transistor_1_out, transistor_2_out, transistor_3_out,
       transistor_4_out, transistor_5_out, transistor_6_out, transistor_7_out, transistor_8_out,
       transistor_9_out, transistor_10_out, transistor_11_out, transistor_12_out, transistor_13_out,
       transistor_14_out, transistor_15_out, transistor_16_out, transistor_17_out, transistor_19_out,
       transistor_20_out, transistor_21_out, transistor_22_out, transistor_23_out, transistor_24_out,
       transistor_25_out, transistor_26_out, transistor_27_out, transistor_28_out, transistor_29_out,
       transistor_30_out, transistor_31_out, transistor_32_out, transistor_33_out, transistor_34_out,
       transistor_35_out, transistor_36_out, transistor_37_out, transistor_38_out, transistor_39_out,
       transistor_40_out, transistor_41_out, transistor_42_out, transistor_43_out, transistor_44_out,
       transistor_45_out, transistor_46_out, transistor_47_out, transistor_48_out, transistor_49_out,
       transistor_50_out, transistor_51_out, transistor_52_out, transistor_53_out, transistor_54_out,
       transistor_55_out, transistor_56_out, transistor_57_out, transistor_58_out, transistor_59_out,
       transistor_60_out, transistor_61_out, transistor_62_out, transistor_63_out, transistor_64_out,
       transistor_65_out, transistor_66_out, transistor_67_out, transistor_68_out, transistor_69_out,
       transistor_70_out, transistor_71_out, transistor_72_out, transistor_73_out, transistor_74_out,
       transistor_75_out, transistor_76_out, transistor_77_out, transistor_78_out, transistor_79_out,
       transistor_80_out, transistor_81_out, transistor_82_out, transistor_83_out, transistor_84_out,
       transistor_85_out, transistor_86_out, transistor_87_out, transistor_88_out, transistor_89_out,
       transistor_90_out, transistor_91_out, transistor_92_out, transistor_93_out, transistor_94_out,
       transistor_95_out, transistor_96_out, transistor_97_out, transistor_98_out, transistor_99_out,
       transistor_100_out, transistor_101_out, transistor_102_out, transistor_103_out, transistor_104_out,
       transistor_105_out, transistor_106_out, transistor_107_out, transistor_108_out, transistor_109_out,
       transistor_110_out, transistor_111_out, transistor_112_out, transistor_113_out, transistor_114_out,
       transistor_115_out, transistor_116_out, transistor_117_out, transistor_118_out, transistor_119_out,
       transistor_120_out, transistor_121_out, transistor_122_out, transistor_123_out, transistor_124_out,
       transistor_126_out, transistor_127_out, transistor_129_out, transistor_130_out, transistor_131_out,
       transistor_132_out, transistor_133_out, transistor_134_out, transistor_136_out, transistor_140_out,
       transistor_142_out, transistor_160_out, transistor_161_out, transistor_162_out, transistor_163_out,
       transistor_164_out, transistor_165_out, transistor_166_out, transistor_167_out, transistor_168_out,
       undriven, undriven_2, undriven_3, undriven_4, undriven_5, undriven_6, undriven_7, undriven_8,
       undriven_9, undriven_10, undriven_11, undriven_12, undriven_13, undriven_14, undriven_15, undriven_16,
       undriven_17, undriven_18, undriven_19, undriven_20, undriven_21, undriven_22, undriven_23,
       undriven_24, undriven_25, undriven_26, undriven_27, undriven_28, undriven_29, undriven_30,
       undriven_31, undriven_32, undriven_33, undriven_34, undriven_35, undriven_36, undriven_37,
       undriven_38, undriven_39, undriven_40, undriven_41, undriven_42, undriven_43, undriven_44,
       undriven_45, undriven_46, undriven_47, undriven_48, undriven_49, undriven_50, undriven_51,
       undriven_52, undriven_53, xor_1_out, xor_2_out, xor_3_out, xor_4_out, xor_5_out, xor_6_out, xor_7_out,
       xor_8_out, xor_9_out, xor_10_out, xor_11_out, xor_12_out, xor_13_out, xor_14_out, xor_15_out,
       xor_16_out, xor_17_out, xor_18_out, xor_19_out, xor_20_out, xor_21_out, xor_22_out, xor_23_out,
       xor_24_out, xor_25_out, xor_26_out, xor_27_out, xor_28_out, xor_29_out, xor_30_out, xor_31_out,
       xor_32_out, xor_33_out, xor_34_out, xor_35_out, xor_36_out, xor_37_out, xor_38_out, xor_39_out,
       xor_40_out, xor_41_out;
  wire [2:0] rom_1_data_2;
  wire [7:0] buffer_201_out, dipswitch_17_sw8, rom_2_data, rom_3_data;
  wire [23:0] rom_1_data, undriven_54;

  xor xor_1 (xor_1_out, undriven_5, undriven);
  and and_1 (and_1_out, undriven_2, undriven_3);
  xor xor_2 (xor_2_out, xor_1_out, or_3_out);
  xor xor_3 (xor_3_out, undriven_9, undriven_10);
  and and_2 (and_2_out, undriven_2, undriven_4);
  and and_3 (and_3_out, xor_1_out, or_3_out);
  xor xor_4 (xor_4_out, xor_3_out, undriven_8);
  and and_4 (and_4_out, undriven_2, undriven_6);
  or or_1 (or_1_out, and_3_out, and_5_out);
  and and_5 (and_5_out, undriven_5, undriven);
  and and_6 (and_6_out, xor_3_out, undriven_8);
  and and_7 (and_7_out, undriven_2, undriven_7);
  xor xor_5 (xor_5_out, undriven_13, undriven_14);
  or or_2 (or_2_out, and_6_out, and_8_out);
  and and_8 (and_8_out, undriven_9, undriven_10);
  and and_9 (and_9_out, undriven_2, undriven_11);
  xor xor_6 (xor_6_out, xor_5_out, or_4_out);
  and and_10 (and_10_out, undriven_2, undriven_12);
  and and_11 (and_11_out, xor_5_out, or_4_out);
  or or_3 (or_3_out, and_11_out, and_12_out);
  and and_12 (and_12_out, undriven_13, undriven_14);
  and and_13 (and_13_out, undriven_2, undriven_15);
  xor xor_7 (xor_7_out, undriven_17, undriven_18);
  and and_14 (and_14_out, undriven_2, undriven_16);
  xor xor_8 (xor_8_out, xor_7_out, or_5_out);
  and and_15 (and_15_out, xor_7_out, or_5_out);
  or or_4 (or_4_out, and_15_out, and_16_out);
  and and_16 (and_16_out, undriven_17, undriven_18);
  xor xor_9 (xor_9_out, undriven_19, undriven_20);
  xor xor_10 (xor_10_out, xor_9_out, or_6_out);
  and and_17 (and_17_out, xor_9_out, or_6_out);
  or or_5 (or_5_out, and_17_out, and_18_out);
  and and_18 (and_18_out, undriven_19, undriven_20);
  xor xor_11 (xor_11_out, undriven_21, undriven_22);
  xor xor_12 (xor_12_out, xor_11_out, or_7_out);
  and and_19 (and_19_out, xor_11_out, or_7_out);
  or or_6 (or_6_out, and_19_out, and_20_out);
  and and_20 (and_20_out, undriven_21, undriven_22);
  xor xor_13 (xor_13_out, undriven_23, undriven_24);
  xor xor_14 (xor_14_out, xor_13_out, or_8_out);
  and and_21 (and_21_out, xor_13_out, or_8_out);
  or or_7 (or_7_out, and_21_out, and_22_out);
  and and_22 (and_22_out, undriven_23, undriven_24);
  xor xor_15 (xor_15_out, undriven_25, undriven_26);
  xor xor_16 (xor_16_out, xor_15_out, and_25_out);
  or or_8 (or_8_out, and_23_out, and_24_out);
  and and_23 (and_23_out, xor_15_out, and_25_out);
  and and_24 (and_24_out, undriven_25, undriven_26);
  xor xor_17 (xor_17_out, undriven_27, undriven_28);
  and and_25 (and_25_out, undriven_27, undriven_28);
  and and_26 (and_26_out, buffer_17_out, transistor_44_out);
  and and_27 (and_27_out, transistor_44_out, transistor_46_out);
  S_R_Flip_Flop s_r_ff_1 (.Q(s_r_ff_1_q), .reset(and_27_out), .preset(and_26_out));  // open: S, R, clk, Qn
  and and_28 (and_28_out, buffer_25_out, transistor_45_out);
  and and_29 (and_29_out, transistor_45_out, transistor_47_out);
  S_R_Flip_Flop s_r_ff_2 (.Q(s_r_ff_2_q), .reset(and_29_out), .preset(and_28_out));  // open: S, R, clk, Qn
  Transistor transistor_1 (.in(undriven_31), .out(transistor_1_out), .gate(1'b0));
  Transistor transistor_2 (.in(undriven_33), .out(transistor_2_out), .gate(1'b0));
  Transistor transistor_3 (.in(undriven_34), .out(transistor_3_out), .gate(1'b0));
  Transistor transistor_4 (.in(undriven_36), .out(transistor_4_out), .gate(1'b0));
  Transistor transistor_5 (.in(undriven_37), .out(transistor_5_out), .gate(1'b0));
  Transistor transistor_6 (.in(undriven_35), .out(transistor_6_out), .gate(1'b0));
  Transistor transistor_7 (.in(undriven_32), .out(transistor_7_out), .gate(1'b0));
  Transistor transistor_8 (.in(undriven_30), .out(transistor_8_out), .gate(1'b0));
  Transistor transistor_9 (.in(undriven_29), .out(transistor_9_out), .gate(1'b0));
  xor xor_18 (xor_18_out, s_r_ff_1_q, xor_20_out);
  xor xor_19 (xor_19_out, xor_18_out, or_10_out);
  xor xor_20 (xor_20_out, dipswitch_3_sw1, s_r_ff_2_q);
  and and_30 (and_30_out, xor_18_out, or_10_out);
  or or_9 (or_9_out, and_30_out, and_31_out);
  and and_31 (and_31_out, s_r_ff_1_q, xor_20_out);
  and and_32 (and_32_out, buffer_18_out, transistor_44_out);
  and and_33 (and_33_out, transistor_44_out, transistor_46_out);
  and and_34 (and_34_out, buffer_26_out, transistor_45_out);
  and and_35 (and_35_out, transistor_45_out, transistor_47_out);
  xor xor_21 (xor_21_out, s_r_ff_3_q, xor_22_out);
  xor xor_22 (xor_22_out, dipswitch_3_sw1, s_r_ff_4_q);
  S_R_Flip_Flop s_r_ff_3 (.Q(s_r_ff_3_q), .reset(and_33_out), .preset(and_32_out));  // open: S, R, clk, Qn
  S_R_Flip_Flop s_r_ff_4 (.Q(s_r_ff_4_q), .reset(and_35_out), .preset(and_34_out));  // open: S, R, clk, Qn
  Transistor transistor_10 (.in(undriven_38), .out(transistor_10_out), .gate(1'b0));
  Transistor transistor_11 (.in(undriven_39), .out(transistor_11_out), .gate(1'b0));
  Transistor transistor_12 (.in(undriven_40), .out(transistor_12_out), .gate(1'b0));
  Transistor transistor_13 (.in(undriven_41), .out(transistor_13_out), .gate(1'b0));
  Transistor transistor_14 (.in(undriven_42), .out(transistor_14_out), .gate(1'b0));
  Transistor transistor_15 (.in(undriven_43), .out(transistor_15_out), .gate(1'b0));
  Transistor transistor_16 (.in(undriven_44), .out(transistor_16_out), .gate(1'b0));
  Transistor transistor_17 (.in(undriven_45), .out(transistor_17_out), .gate(1'b0));
  xor xor_23 (xor_23_out, xor_21_out, or_11_out);
  or or_10 (or_10_out, and_36_out, and_37_out);
  and and_36 (and_36_out, xor_21_out, or_11_out);
  and and_37 (and_37_out, s_r_ff_3_q, xor_22_out);
  xor xor_24 (xor_24_out, s_r_ff_5_q, xor_25_out);
  xor xor_25 (xor_25_out, dipswitch_3_sw1, s_r_ff_6_q);
  and and_38 (and_38_out, buffer_19_out, transistor_44_out);
  and and_39 (and_39_out, transistor_44_out, transistor_46_out);
  and and_40 (and_40_out, buffer_27_out, transistor_45_out);
  and and_41 (and_41_out, transistor_45_out, transistor_47_out);
  xor xor_26 (xor_26_out, xor_24_out, or_12_out);
  S_R_Flip_Flop s_r_ff_5 (.Q(s_r_ff_5_q), .reset(and_39_out), .preset(and_38_out));  // open: S, R, clk, Qn
  S_R_Flip_Flop s_r_ff_6 (.Q(s_r_ff_6_q), .reset(and_41_out), .preset(and_40_out));  // open: S, R, clk, Qn
  and and_42 (and_42_out, xor_24_out, or_12_out);
  or or_11 (or_11_out, and_42_out, and_43_out);
  and and_43 (and_43_out, s_r_ff_5_q, xor_25_out);
  xor xor_27 (xor_27_out, s_r_ff_7_q, xor_28_out);
  xor xor_28 (xor_28_out, dipswitch_3_sw1, s_r_ff_8_q);
  and and_44 (and_44_out, buffer_20_out, transistor_44_out);
  and and_45 (and_45_out, transistor_44_out, transistor_46_out);
  and and_46 (and_46_out, buffer_28_out, transistor_45_out);
  and and_47 (and_47_out, transistor_45_out, transistor_47_out);
  xor xor_29 (xor_29_out, xor_27_out, or_13_out);
  S_R_Flip_Flop s_r_ff_7 (.Q(s_r_ff_7_q), .reset(and_45_out), .preset(and_44_out));  // open: S, R, clk, Qn
  S_R_Flip_Flop s_r_ff_8 (.Q(s_r_ff_8_q), .reset(and_47_out), .preset(and_46_out));  // open: S, R, clk, Qn
  or or_12 (or_12_out, and_48_out, and_49_out);
  and and_48 (and_48_out, xor_27_out, or_13_out);
  and and_49 (and_49_out, s_r_ff_7_q, xor_28_out);
  xor xor_30 (xor_30_out, s_r_ff_9_q, xor_31_out);
  xor xor_31 (xor_31_out, dipswitch_3_sw1, s_r_ff_10_q);
  and and_50 (and_50_out, buffer_21_out, transistor_44_out);
  and and_51 (and_51_out, transistor_44_out, transistor_46_out);
  J_K_Flip_Flop j_k_ff_1 (
    .J(1'b1), .K(1'b1), .clk(j_k_ff_2_q), .Q(j_k_ff_1_q), .reset(button_2_out));  // open: Qn, preset
  xor xor_32 (xor_32_out, xor_30_out, or_14_out);
  S_R_Flip_Flop s_r_ff_9 (.Q(s_r_ff_9_q), .reset(and_51_out), .preset(and_50_out));  // open: S, R, clk, Qn
  and and_52 (and_52_out, buffer_29_out, transistor_45_out);
  and and_53 (and_53_out, transistor_45_out, transistor_47_out);
  or or_13 (or_13_out, and_54_out, and_55_out);
  and and_54 (and_54_out, xor_30_out, or_14_out);
  S_R_Flip_Flop s_r_ff_10 (.Q(s_r_ff_10_q), .reset(and_53_out), .preset(and_52_out));  // open: S, R, clk, Qn
  buf buffer_1 (buffer_1_out, undriven_46);
  buf buffer_2 (buffer_2_out, undriven_47);
  buf buffer_3 (buffer_3_out, undriven_48);
  buf buffer_4 (buffer_4_out, undriven_49);
  buf buffer_5 (buffer_5_out, undriven_50);
  buf buffer_6 (buffer_6_out, undriven_51);
  buf buffer_7 (buffer_7_out, undriven_52);
  buf buffer_8 (buffer_8_out, undriven_53);
  J_K_Flip_Flop j_k_ff_2 (
    .J(1'b1), .K(1'b1), .clk(j_k_ff_3_q), .Q(j_k_ff_2_q), .reset(button_2_out));  // open: Qn, preset
  and and_55 (and_55_out, s_r_ff_9_q, xor_31_out);
  xor xor_33 (xor_33_out, s_r_ff_11_q, xor_34_out);
  xor xor_34 (xor_34_out, dipswitch_3_sw1, s_r_ff_12_q);
  // Buffer buffer_9 is placed but not wired
  // Buffer buffer_10 is placed but not wired
  // Buffer buffer_11 is placed but not wired
  // Buffer buffer_12 is placed but not wired
  // Buffer buffer_13 is placed but not wired
  // Buffer buffer_14 is placed but not wired
  // Buffer buffer_15 is placed but not wired
  // Buffer buffer_16 is placed but not wired
  J_K_Flip_Flop j_k_ff_3 (
    .J(1'b1), .K(1'b1), .clk(j_k_ff_4_q), .Q(j_k_ff_3_q), .reset(button_2_out));  // open: Qn, preset
  xor xor_35 (xor_35_out, xor_33_out, or_15_out);
  and and_56 (and_56_out, xor_33_out, or_15_out);
  and and_57 (and_57_out, buffer_22_out, transistor_44_out);
  and and_58 (and_58_out, transistor_44_out, transistor_46_out);
  and and_59 (and_59_out, buffer_30_out, transistor_45_out);
  and and_60 (and_60_out, transistor_45_out, transistor_47_out);
  J_K_Flip_Flop j_k_ff_4 (
    .J(1'b1), .K(1'b1), .clk(j_k_ff_5_q), .Q(j_k_ff_4_q), .reset(button_2_out));  // open: Qn, preset
  or or_14 (or_14_out, and_56_out, and_61_out);
  and and_61 (and_61_out, s_r_ff_11_q, xor_34_out);
  S_R_Flip_Flop s_r_ff_11 (.Q(s_r_ff_11_q), .reset(and_58_out), .preset(and_57_out));  // open: S, R, clk, Qn
  S_R_Flip_Flop s_r_ff_12 (.Q(s_r_ff_12_q), .reset(and_60_out), .preset(and_59_out));  // open: S, R, clk, Qn
  J_K_Flip_Flop j_k_ff_5 (
    .J(1'b1), .K(1'b1), .clk(j_k_ff_6_q), .Q(j_k_ff_5_q), .reset(button_2_out));  // open: Qn, preset
  xor xor_36 (xor_36_out, s_r_ff_13_q, xor_37_out);
  xor xor_37 (xor_37_out, dipswitch_3_sw1, s_r_ff_14_q);
  J_K_Flip_Flop j_k_ff_6 (
    .J(1'b1), .K(1'b1), .clk(j_k_ff_7_q), .Q(j_k_ff_6_q), .reset(button_2_out));  // open: Qn, preset
  xor xor_38 (xor_38_out, xor_36_out, or_16_out);
  or or_15 (or_15_out, and_62_out, and_67_out);
  and and_62 (and_62_out, xor_36_out, or_16_out);
  and and_63 (and_63_out, buffer_23_out, transistor_44_out);
  and and_64 (and_64_out, transistor_44_out, transistor_46_out);
  and and_65 (and_65_out, buffer_31_out, transistor_45_out);
  and and_66 (and_66_out, transistor_45_out, transistor_47_out);
  J_K_Flip_Flop j_k_ff_7 (
    .J(1'b1), .K(1'b1), .clk(j_k_ff_8_q), .Q(j_k_ff_7_q), .reset(button_2_out));  // open: Qn, preset
  and and_67 (and_67_out, s_r_ff_13_q, xor_37_out);
  S_R_Flip_Flop s_r_ff_13 (.Q(s_r_ff_13_q), .reset(and_64_out), .preset(and_63_out));  // open: S, R, clk, Qn
  S_R_Flip_Flop s_r_ff_14 (.Q(s_r_ff_14_q), .reset(and_66_out), .preset(and_65_out));  // open: S, R, clk, Qn
  DipSwitch dipswitch_1 (
    .sw1(dipswitch_1_sw1), .sw2(dipswitch_1_sw2), .sw3(dipswitch_1_sw3), .sw4(dipswitch_1_sw4),
    .sw5(dipswitch_1_sw5), .sw6(dipswitch_1_sw6), .sw7(dipswitch_1_sw7), .sw8(dipswitch_1_sw8));
  Button button_1 (.out(button_1_out));
  xor xor_39 (xor_39_out, s_r_ff_15_q, xor_40_out);
  xor xor_40 (xor_40_out, dipswitch_3_sw1, s_r_ff_16_q);
  J_K_Flip_Flop j_k_ff_8 (
    .J(1'b1), .K(1'b1), .clk(digital_oscilloscope_1_p1), .Q(j_k_ff_8_q), .reset(button_2_out));  // open: Qn, preset
  xor xor_41 (xor_41_out, xor_39_out, dipswitch_3_sw1);
  Clock clock_1 (.out(clock_1_out));
  DipSwitch dipswitch_2 (.sw8(dipswitch_2_sw8));  // open: sw1, sw2, sw3, sw4, sw5, sw6, sw7
  Button button_2 (.out(button_2_out));
  // Digital_Oscilloscope digital_oscilloscope_1: pin names not known; wires that end beside it: digital_oscilloscope_1_p1, digital_oscilloscope_1_p2
  or or_16 (or_16_out, and_68_out, and_77_out);
  and and_68 (and_68_out, xor_39_out, dipswitch_3_sw1);
  and and_69 (and_69_out, dipswitch_1_sw1, button_1_out);
  and and_70 (and_70_out, dipswitch_1_sw2, button_1_out);
  and and_71 (and_71_out, dipswitch_1_sw3, button_1_out);
  and and_72 (and_72_out, dipswitch_1_sw4, button_1_out);
  and and_73 (and_73_out, dipswitch_1_sw5, button_1_out);
  and and_74 (and_74_out, dipswitch_1_sw6, button_1_out);
  and and_75 (and_75_out, dipswitch_1_sw7, button_1_out);
  and and_76 (and_76_out, dipswitch_1_sw8, button_1_out);
  LedBar ledbar_1 (
    .led0(not_1_out), .led1(not_2_out), .led2(not_3_out), .led3(not_4_out), .led4(not_5_out),
    .led5(not_6_out), .led6(not_7_out), .led7(digital_oscilloscope_1_p2));
  not not_1 (not_1_out, j_k_ff_1_q);
  not not_2 (not_2_out, j_k_ff_2_q);
  not not_3 (not_3_out, j_k_ff_3_q);
  not not_4 (not_4_out, j_k_ff_4_q);
  not not_5 (not_5_out, j_k_ff_5_q);
  not not_6 (not_6_out, j_k_ff_6_q);
  not not_7 (not_7_out, j_k_ff_7_q);
  not not_8 (digital_oscilloscope_1_p2, j_k_ff_8_q);
  // Switch switch_1: pin names not known; wires that end beside it: 1'b1, clock_1_out, digital_oscilloscope_1_p1
  and and_77 (and_77_out, s_r_ff_15_q, xor_40_out);
  and and_78 (and_78_out, buffer_24_out, transistor_44_out);
  and and_79 (and_79_out, transistor_44_out, transistor_46_out);
  and and_80 (and_80_out, buffer_32_out, transistor_45_out);
  and and_81 (and_81_out, transistor_45_out, transistor_47_out);
  S_R_Flip_Flop s_r_ff_15 (.Q(s_r_ff_15_q), .reset(and_79_out), .preset(and_78_out));  // open: S, R, clk, Qn
  S_R_Flip_Flop s_r_ff_16 (.Q(s_r_ff_16_q), .reset(and_81_out), .preset(and_80_out));  // open: S, R, clk, Qn
  and and_82 (and_82_out, xor_19_out, rom_1_data[18]);
  and and_83 (and_83_out, xor_23_out, rom_1_data[18]);
  and and_84 (and_84_out, xor_26_out, rom_1_data[18]);
  and and_85 (and_85_out, xor_29_out, rom_1_data[18]);
  and and_86 (and_86_out, xor_32_out, rom_1_data[18]);
  and and_87 (and_87_out, xor_35_out, rom_1_data[18]);
  and and_88 (and_88_out, xor_38_out, rom_1_data[18]);
  and and_89 (and_89_out, xor_41_out, rom_1_data[18]);
  LedBar ledbar_2 (
    .led0(buffer_17_out), .led1(buffer_18_out), .led2(buffer_19_out), .led3(buffer_20_out),
    .led4(buffer_21_out), .led5(buffer_22_out), .led6(buffer_23_out), .led7(buffer_24_out));
  LedBar ledbar_3 (
    .led0(buffer_25_out), .led1(buffer_26_out), .led2(buffer_27_out), .led3(buffer_28_out),
    .led4(buffer_29_out), .led5(buffer_30_out), .led6(buffer_31_out), .led7(buffer_32_out));
  and and_90 (and_90_out, not_1_out, dipswitch_2_sw8);
  and and_91 (and_91_out, not_2_out, dipswitch_2_sw8);
  and and_92 (and_92_out, not_3_out, dipswitch_2_sw8);
  and and_93 (and_93_out, not_4_out, dipswitch_2_sw8);
  and and_94 (and_94_out, not_5_out, dipswitch_2_sw8);
  and and_95 (and_95_out, not_6_out, dipswitch_2_sw8);
  and and_96 (and_96_out, not_7_out, dipswitch_2_sw8);
  and and_97 (and_97_out, digital_oscilloscope_1_p2, dipswitch_2_sw8);
  LedBar ledbar_4 (
    .led0(and_82_out), .led1(and_83_out), .led2(and_84_out), .led3(and_85_out), .led4(and_86_out),
    .led5(and_87_out), .led6(and_88_out), .led7(and_89_out));
  Transistor transistor_18 (.in(button_3_out), .out(rom_1_data[18]), .gate(1'b0));
  Button button_3 (.out(button_3_out));
  Transistor transistor_19 (.in(and_69_out), .out(transistor_19_out), .gate(1'b0));
  Transistor transistor_20 (.in(and_70_out), .out(transistor_20_out), .gate(1'b0));
  Transistor transistor_21 (.in(and_71_out), .out(transistor_21_out), .gate(1'b0));
  Transistor transistor_22 (.in(and_72_out), .out(transistor_22_out), .gate(1'b0));
  Transistor transistor_23 (.in(and_73_out), .out(transistor_23_out), .gate(1'b0));
  Transistor transistor_24 (.in(and_74_out), .out(transistor_24_out), .gate(1'b0));
  Transistor transistor_25 (.in(and_75_out), .out(transistor_25_out), .gate(1'b0));
  Transistor transistor_26 (.in(and_76_out), .out(transistor_26_out), .gate(1'b0));
  Transistor transistor_27 (.in(and_90_out), .out(transistor_27_out), .gate(1'b0));
  Transistor transistor_28 (.in(and_91_out), .out(transistor_28_out), .gate(1'b0));
  Transistor transistor_29 (.in(and_92_out), .out(transistor_29_out), .gate(1'b0));
  Transistor transistor_30 (.in(and_93_out), .out(transistor_30_out), .gate(1'b0));
  Transistor transistor_31 (.in(and_94_out), .out(transistor_31_out), .gate(1'b0));
  Transistor transistor_32 (.in(and_95_out), .out(transistor_32_out), .gate(1'b0));
  Transistor transistor_33 (.in(and_96_out), .out(transistor_33_out), .gate(1'b0));
  Transistor transistor_34 (.in(and_97_out), .out(transistor_34_out), .gate(1'b0));
  Transistor transistor_35 (.in(or_9_out), .out(transistor_35_out), .gate(1'b0));
  Transistor transistor_36 (.in(and_82_out), .out(transistor_36_out), .gate(1'b0));
  Transistor transistor_37 (.in(and_83_out), .out(transistor_37_out), .gate(1'b0));
  Transistor transistor_38 (.in(and_84_out), .out(transistor_38_out), .gate(1'b0));
  Transistor transistor_39 (.in(and_85_out), .out(transistor_39_out), .gate(1'b0));
  Transistor transistor_40 (.in(and_86_out), .out(transistor_40_out), .gate(1'b0));
  Transistor transistor_41 (.in(and_87_out), .out(transistor_41_out), .gate(1'b0));
  Transistor transistor_42 (.in(and_88_out), .out(transistor_42_out), .gate(1'b0));
  Transistor transistor_43 (.in(and_89_out), .out(transistor_43_out), .gate(1'b0));
  Transistor transistor_44 (.in(dipswitch_4_sw1), .out(transistor_44_out), .gate(1'b0));
  Transistor transistor_45 (.in(dipswitch_5_sw1), .out(transistor_45_out), .gate(1'b0));
  LedBar ledbar_5 (
    .led0(buffer_65_out), .led1(buffer_64_out), .led2(buffer_63_out), .led3(buffer_62_out),
    .led4(buffer_61_out), .led5(buffer_60_out), .led6(buffer_59_out), .led7(buffer_58_out));
  buf buffer_17 (buffer_17_out, buffer_49_out);
  buf buffer_18 (buffer_18_out, buffer_48_out);
  buf buffer_19 (buffer_19_out, buffer_47_out);
  buf buffer_20 (buffer_20_out, buffer_46_out);
  buf buffer_21 (buffer_21_out, buffer_45_out);
  buf buffer_22 (buffer_22_out, buffer_44_out);
  buf buffer_23 (buffer_23_out, buffer_43_out);
  buf buffer_24 (buffer_24_out, buffer_42_out);
  buf buffer_25 (buffer_25_out, buffer_49_out);
  buf buffer_26 (buffer_26_out, buffer_48_out);
  buf buffer_27 (buffer_27_out, buffer_47_out);
  buf buffer_28 (buffer_28_out, buffer_46_out);
  buf buffer_29 (buffer_29_out, buffer_45_out);
  buf buffer_30 (buffer_30_out, buffer_44_out);
  buf buffer_31 (buffer_31_out, buffer_43_out);
  buf buffer_32 (buffer_32_out, buffer_42_out);
  buf buffer_33 (buffer_33_out, transistor_27_out);
  buf buffer_34 (buffer_34_out, transistor_28_out);
  buf buffer_35 (buffer_35_out, transistor_29_out);
  buf buffer_36 (buffer_36_out, transistor_30_out);
  buf buffer_37 (buffer_37_out, transistor_31_out);
  buf buffer_38 (buffer_38_out, transistor_32_out);
  buf buffer_39 (buffer_39_out, transistor_33_out);
  buf buffer_40 (buffer_40_out, transistor_34_out);
  buf buffer_41 (buffer_41_out, transistor_35_out);
  buf buffer_42 (buffer_42_out, transistor_36_out);
  buf buffer_43 (buffer_43_out, transistor_37_out);
  buf buffer_44 (buffer_44_out, transistor_38_out);
  buf buffer_45 (buffer_45_out, transistor_39_out);
  buf buffer_46 (buffer_46_out, transistor_40_out);
  buf buffer_47 (buffer_47_out, transistor_41_out);
  buf buffer_48 (buffer_48_out, transistor_42_out);
  buf buffer_49 (buffer_49_out, transistor_43_out);
  DipSwitch dipswitch_3 (.sw1(dipswitch_3_sw1));  // open: sw2, sw3, sw4, sw5, sw6, sw7, sw8
  DipSwitch dipswitch_4 (.sw1(dipswitch_4_sw1));  // open: sw2, sw3, sw4, sw5, sw6, sw7, sw8
  DipSwitch dipswitch_5 (.sw1(dipswitch_5_sw1));  // open: sw2, sw3, sw4, sw5, sw6, sw7, sw8
  buf buffer_50 (buffer_49_out, transistor_19_out);
  buf buffer_51 (buffer_48_out, transistor_20_out);
  buf buffer_52 (buffer_47_out, transistor_21_out);
  buf buffer_53 (buffer_46_out, transistor_22_out);
  buf buffer_54 (buffer_54_out, transistor_23_out);
  buf buffer_55 (buffer_44_out, transistor_24_out);
  buf buffer_56 (buffer_43_out, transistor_25_out);
  buf buffer_57 (buffer_42_out, transistor_26_out);
  buf buffer_58 (buffer_58_out, buffer_42_out);
  buf buffer_59 (buffer_59_out, buffer_43_out);
  buf buffer_60 (buffer_60_out, buffer_44_out);
  buf buffer_61 (buffer_61_out, buffer_45_out);
  buf buffer_62 (buffer_62_out, buffer_46_out);
  buf buffer_63 (buffer_63_out, buffer_47_out);
  buf buffer_64 (buffer_64_out, buffer_48_out);
  buf buffer_65 (buffer_65_out, buffer_49_out);
  Transistor transistor_46 (.in(button_4_out), .out(transistor_46_out), .gate(1'b0));
  Button button_4 (.out(button_4_out));
  Transistor transistor_47 (.in(button_5_out), .out(transistor_47_out), .gate(1'b0));
  Button button_5 (.out(button_5_out));
  LED led_1 (.in(buffer_41_out));
  LedBar ledbar_6 (
    .led0(buffer_40_out), .led1(buffer_39_out), .led2(buffer_38_out), .led3(buffer_37_out),
    .led4(buffer_36_out), .led5(buffer_35_out), .led6(buffer_34_out), .led7(buffer_33_out));
  buf buffer_66 (buffer_42_out, transistor_48_out);
  buf buffer_67 (buffer_43_out, transistor_49_out);
  buf buffer_68 (buffer_44_out, transistor_50_out);
  buf buffer_69 (buffer_45_out, transistor_51_out);
  buf buffer_70 (buffer_46_out, transistor_52_out);
  buf buffer_71 (buffer_47_out, transistor_53_out);
  buf buffer_72 (buffer_48_out, transistor_54_out);
  buf buffer_73 (buffer_49_out, transistor_55_out);
  buf buffer_74 (buffer_74_out, buffer_42_out);
  buf buffer_75 (buffer_75_out, buffer_43_out);
  buf buffer_76 (buffer_76_out, buffer_44_out);
  buf buffer_77 (buffer_77_out, buffer_45_out);
  buf buffer_78 (buffer_78_out, buffer_46_out);
  buf buffer_79 (buffer_79_out, buffer_47_out);
  buf buffer_80 (buffer_80_out, buffer_48_out);
  buf buffer_81 (buffer_81_out, buffer_49_out);
  buf buffer_82 (buffer_42_out, transistor_56_out);
  buf buffer_83 (buffer_43_out, transistor_57_out);
  buf buffer_84 (buffer_44_out, transistor_58_out);
  buf buffer_85 (buffer_45_out, transistor_59_out);
  buf buffer_86 (buffer_46_out, transistor_60_out);
  buf buffer_87 (buffer_47_out, transistor_61_out);
  buf buffer_88 (buffer_48_out, transistor_62_out);
  buf buffer_89 (buffer_49_out, transistor_63_out);
  buf buffer_90 (buffer_90_out, buffer_42_out);
  buf buffer_91 (buffer_91_out, buffer_43_out);
  buf buffer_92 (buffer_92_out, buffer_44_out);
  buf buffer_93 (buffer_93_out, buffer_45_out);
  buf buffer_94 (buffer_94_out, buffer_46_out);
  buf buffer_95 (buffer_95_out, buffer_47_out);
  buf buffer_96 (buffer_96_out, buffer_48_out);
  buf buffer_97 (buffer_97_out, buffer_49_out);
  buf buffer_98 (buffer_42_out, transistor_64_out);
  buf buffer_99 (buffer_43_out, transistor_65_out);
  buf buffer_100 (buffer_44_out, transistor_66_out);
  buf buffer_101 (buffer_45_out, transistor_67_out);
  buf buffer_102 (buffer_46_out, transistor_68_out);
  buf buffer_103 (buffer_47_out, transistor_69_out);
  buf buffer_104 (buffer_48_out, transistor_70_out);
  buf buffer_105 (buffer_49_out, transistor_71_out);
  buf buffer_106 (buffer_106_out, buffer_42_out);
  buf buffer_107 (buffer_107_out, buffer_43_out);
  buf buffer_108 (buffer_108_out, buffer_44_out);
  buf buffer_109 (buffer_109_out, buffer_45_out);
  buf buffer_110 (buffer_110_out, buffer_46_out);
  buf buffer_111 (buffer_111_out, buffer_47_out);
  buf buffer_112 (buffer_112_out, buffer_48_out);
  buf buffer_113 (buffer_113_out, buffer_49_out);
  buf buffer_114 (buffer_42_out, transistor_72_out);
  buf buffer_115 (buffer_43_out, transistor_73_out);
  buf buffer_116 (buffer_44_out, transistor_74_out);
  buf buffer_117 (buffer_45_out, transistor_75_out);
  buf buffer_118 (buffer_46_out, transistor_76_out);
  buf buffer_119 (buffer_47_out, transistor_77_out);
  buf buffer_120 (buffer_48_out, transistor_78_out);
  buf buffer_121 (buffer_49_out, transistor_79_out);
  buf buffer_122 (buffer_122_out, buffer_42_out);
  buf buffer_123 (buffer_123_out, buffer_43_out);
  buf buffer_124 (buffer_124_out, buffer_44_out);
  buf buffer_125 (buffer_125_out, buffer_45_out);
  buf buffer_126 (buffer_126_out, buffer_46_out);
  buf buffer_127 (buffer_127_out, buffer_47_out);
  buf buffer_128 (buffer_128_out, buffer_48_out);
  buf buffer_129 (buffer_129_out, buffer_49_out);
  buf buffer_130 (buffer_42_out, transistor_80_out);
  buf buffer_131 (buffer_43_out, transistor_81_out);
  buf buffer_132 (buffer_44_out, transistor_82_out);
  buf buffer_133 (buffer_45_out, transistor_83_out);
  buf buffer_134 (buffer_46_out, transistor_84_out);
  buf buffer_135 (buffer_47_out, transistor_85_out);
  buf buffer_136 (buffer_48_out, transistor_86_out);
  buf buffer_137 (buffer_49_out, transistor_87_out);
  buf buffer_138 (buffer_138_out, buffer_42_out);
  buf buffer_139 (buffer_139_out, buffer_43_out);
  buf buffer_140 (buffer_140_out, buffer_44_out);
  buf buffer_141 (buffer_141_out, buffer_45_out);
  buf buffer_142 (buffer_142_out, buffer_46_out);
  buf buffer_143 (buffer_143_out, buffer_47_out);
  buf buffer_144 (buffer_144_out, buffer_48_out);
  buf buffer_145 (buffer_145_out, buffer_49_out);
  buf buffer_146 (buffer_42_out, transistor_88_out);
  buf buffer_147 (buffer_43_out, transistor_89_out);
  buf buffer_148 (buffer_44_out, transistor_90_out);
  buf buffer_149 (buffer_45_out, transistor_91_out);
  buf buffer_150 (buffer_46_out, transistor_92_out);
  buf buffer_151 (buffer_47_out, transistor_93_out);
  buf buffer_152 (buffer_48_out, transistor_94_out);
  buf buffer_153 (buffer_49_out, transistor_95_out);
  buf buffer_154 (buffer_154_out, buffer_42_out);
  buf buffer_155 (buffer_155_out, buffer_43_out);
  buf buffer_156 (buffer_156_out, buffer_44_out);
  buf buffer_157 (buffer_157_out, buffer_45_out);
  buf buffer_158 (buffer_158_out, buffer_46_out);
  buf buffer_159 (buffer_159_out, buffer_47_out);
  buf buffer_160 (buffer_160_out, buffer_48_out);
  buf buffer_161 (buffer_161_out, buffer_49_out);
  buf buffer_162 (buffer_42_out, transistor_96_out);
  buf buffer_163 (buffer_43_out, transistor_97_out);
  buf buffer_164 (buffer_44_out, transistor_98_out);
  buf buffer_165 (buffer_45_out, transistor_99_out);
  buf buffer_166 (buffer_46_out, transistor_100_out);
  buf buffer_167 (buffer_47_out, transistor_101_out);
  buf buffer_168 (buffer_48_out, transistor_102_out);
  buf buffer_169 (buffer_49_out, transistor_103_out);
  buf buffer_170 (buffer_170_out, buffer_42_out);
  buf buffer_171 (buffer_171_out, buffer_43_out);
  buf buffer_172 (buffer_172_out, buffer_44_out);
  buf buffer_173 (buffer_173_out, buffer_45_out);
  buf buffer_174 (buffer_174_out, buffer_46_out);
  buf buffer_175 (buffer_175_out, buffer_47_out);
  buf buffer_176 (buffer_176_out, buffer_48_out);
  buf buffer_177 (buffer_177_out, buffer_49_out);
  buf buffer_178 (buffer_42_out, transistor_104_out);
  buf buffer_179 (buffer_43_out, transistor_105_out);
  buf buffer_180 (buffer_44_out, transistor_106_out);
  buf buffer_181 (buffer_45_out, transistor_107_out);
  buf buffer_182 (buffer_46_out, transistor_108_out);
  buf buffer_183 (buffer_47_out, transistor_109_out);
  buf buffer_184 (buffer_48_out, transistor_110_out);
  buf buffer_185 (buffer_49_out, transistor_111_out);
  buf buffer_186 (buffer_186_out, buffer_42_out);
  buf buffer_187 (buffer_187_out, buffer_43_out);
  buf buffer_188 (buffer_188_out, buffer_44_out);
  buf buffer_189 (buffer_189_out, buffer_45_out);
  buf buffer_190 (buffer_190_out, buffer_46_out);
  buf buffer_191 (buffer_191_out, buffer_47_out);
  buf buffer_192 (buffer_192_out, buffer_48_out);
  buf buffer_193 (buffer_193_out, buffer_49_out);
  Transistor transistor_48 (.in(and_106_out), .out(transistor_48_out), .gate(1'b0));
  Transistor transistor_49 (.in(and_107_out), .out(transistor_49_out), .gate(1'b0));
  Transistor transistor_50 (.in(and_108_out), .out(transistor_50_out), .gate(1'b0));
  Transistor transistor_51 (.in(and_109_out), .out(transistor_51_out), .gate(1'b0));
  Transistor transistor_52 (.in(and_110_out), .out(transistor_52_out), .gate(1'b0));
  Transistor transistor_53 (.in(and_111_out), .out(transistor_53_out), .gate(1'b0));
  Transistor transistor_54 (.in(and_112_out), .out(transistor_54_out), .gate(1'b0));
  Transistor transistor_55 (.in(and_113_out), .out(transistor_55_out), .gate(1'b0));
  Transistor transistor_56 (.in(and_146_out), .out(transistor_56_out), .gate(1'b0));
  Transistor transistor_57 (.in(and_147_out), .out(transistor_57_out), .gate(1'b0));
  Transistor transistor_58 (.in(and_148_out), .out(transistor_58_out), .gate(1'b0));
  Transistor transistor_59 (.in(and_149_out), .out(transistor_59_out), .gate(1'b0));
  Transistor transistor_60 (.in(and_150_out), .out(transistor_60_out), .gate(1'b0));
  Transistor transistor_61 (.in(and_151_out), .out(transistor_61_out), .gate(1'b0));
  Transistor transistor_62 (.in(and_152_out), .out(transistor_62_out), .gate(1'b0));
  Transistor transistor_63 (.in(and_153_out), .out(transistor_63_out), .gate(1'b0));
  Transistor transistor_64 (.in(and_114_out), .out(transistor_64_out), .gate(1'b0));
  Transistor transistor_65 (.in(and_115_out), .out(transistor_65_out), .gate(1'b0));
  Transistor transistor_66 (.in(and_116_out), .out(transistor_66_out), .gate(1'b0));
  Transistor transistor_67 (.in(and_117_out), .out(transistor_67_out), .gate(1'b0));
  Transistor transistor_68 (.in(and_118_out), .out(transistor_68_out), .gate(1'b0));
  Transistor transistor_69 (.in(and_119_out), .out(transistor_69_out), .gate(1'b0));
  Transistor transistor_70 (.in(and_120_out), .out(transistor_70_out), .gate(1'b0));
  Transistor transistor_71 (.in(and_121_out), .out(transistor_71_out), .gate(1'b0));
  Transistor transistor_72 (.in(and_154_out), .out(transistor_72_out), .gate(1'b0));
  Transistor transistor_73 (.in(and_155_out), .out(transistor_73_out), .gate(1'b0));
  Transistor transistor_74 (.in(and_156_out), .out(transistor_74_out), .gate(1'b0));
  Transistor transistor_75 (.in(and_157_out), .out(transistor_75_out), .gate(1'b0));
  Transistor transistor_76 (.in(and_158_out), .out(transistor_76_out), .gate(1'b0));
  Transistor transistor_77 (.in(and_159_out), .out(transistor_77_out), .gate(1'b0));
  Transistor transistor_78 (.in(and_160_out), .out(transistor_78_out), .gate(1'b0));
  Transistor transistor_79 (.in(and_161_out), .out(transistor_79_out), .gate(1'b0));
  Transistor transistor_80 (.in(and_122_out), .out(transistor_80_out), .gate(1'b0));
  Transistor transistor_81 (.in(and_123_out), .out(transistor_81_out), .gate(1'b0));
  Transistor transistor_82 (.in(and_124_out), .out(transistor_82_out), .gate(1'b0));
  Transistor transistor_83 (.in(and_125_out), .out(transistor_83_out), .gate(1'b0));
  Transistor transistor_84 (.in(and_126_out), .out(transistor_84_out), .gate(1'b0));
  Transistor transistor_85 (.in(and_127_out), .out(transistor_85_out), .gate(1'b0));
  Transistor transistor_86 (.in(and_128_out), .out(transistor_86_out), .gate(1'b0));
  Transistor transistor_87 (.in(and_129_out), .out(transistor_87_out), .gate(1'b0));
  Transistor transistor_88 (.in(and_130_out), .out(transistor_88_out), .gate(1'b0));
  Transistor transistor_89 (.in(and_131_out), .out(transistor_89_out), .gate(1'b0));
  Transistor transistor_90 (.in(and_132_out), .out(transistor_90_out), .gate(1'b0));
  Transistor transistor_91 (.in(and_133_out), .out(transistor_91_out), .gate(1'b0));
  Transistor transistor_92 (.in(and_134_out), .out(transistor_92_out), .gate(1'b0));
  Transistor transistor_93 (.in(and_135_out), .out(transistor_93_out), .gate(1'b0));
  Transistor transistor_94 (.in(and_136_out), .out(transistor_94_out), .gate(1'b0));
  Transistor transistor_95 (.in(and_137_out), .out(transistor_95_out), .gate(1'b0));
  Transistor transistor_96 (.in(and_138_out), .out(transistor_96_out), .gate(1'b0));
  Transistor transistor_97 (.in(and_139_out), .out(transistor_97_out), .gate(1'b0));
  Transistor transistor_98 (.in(and_140_out), .out(transistor_98_out), .gate(1'b0));
  Transistor transistor_99 (.in(and_141_out), .out(transistor_99_out), .gate(1'b0));
  Transistor transistor_100 (.in(and_142_out), .out(transistor_100_out), .gate(1'b0));
  Transistor transistor_101 (.in(and_143_out), .out(transistor_101_out), .gate(1'b0));
  Transistor transistor_102 (.in(and_144_out), .out(transistor_102_out), .gate(1'b0));
  Transistor transistor_103 (.in(and_145_out), .out(transistor_103_out), .gate(1'b0));
  Transistor transistor_104 (.in(and_98_out), .out(transistor_104_out), .gate(1'b0));
  Transistor transistor_105 (.in(and_99_out), .out(transistor_105_out), .gate(1'b0));
  Transistor transistor_106 (.in(and_100_out), .out(transistor_106_out), .gate(1'b0));
  Transistor transistor_107 (.in(and_101_out), .out(transistor_107_out), .gate(1'b0));
  Transistor transistor_108 (.in(and_102_out), .out(transistor_108_out), .gate(1'b0));
  Transistor transistor_109 (.in(and_103_out), .out(transistor_109_out), .gate(1'b0));
  Transistor transistor_110 (.in(and_104_out), .out(transistor_110_out), .gate(1'b0));
  Transistor transistor_111 (.in(and_105_out), .out(transistor_111_out), .gate(1'b0));
  and and_98 (and_98_out, s_r_ff_80_q, transistor_112_out);
  and and_99 (and_99_out, s_r_ff_72_q, transistor_112_out);
  and and_100 (and_100_out, s_r_ff_64_q, transistor_112_out);
  and and_101 (and_101_out, s_r_ff_56_q, transistor_112_out);
  and and_102 (and_102_out, s_r_ff_48_q, transistor_112_out);
  and and_103 (and_103_out, s_r_ff_40_q, transistor_112_out);
  and and_104 (and_104_out, s_r_ff_32_q, transistor_112_out);
  and and_105 (and_105_out, s_r_ff_24_q, transistor_112_out);
  and and_106 (and_106_out, s_r_ff_73_q, transistor_113_out);
  and and_107 (and_107_out, s_r_ff_65_q, transistor_113_out);
  and and_108 (and_108_out, s_r_ff_57_q, transistor_113_out);
  and and_109 (and_109_out, s_r_ff_49_q, transistor_113_out);
  and and_110 (and_110_out, s_r_ff_41_q, transistor_113_out);
  and and_111 (and_111_out, s_r_ff_33_q, transistor_113_out);
  and and_112 (and_112_out, s_r_ff_25_q, transistor_113_out);
  and and_113 (and_113_out, s_r_ff_17_q, transistor_113_out);
  and and_114 (and_114_out, s_r_ff_75_q, transistor_115_out);
  and and_115 (and_115_out, s_r_ff_67_q, transistor_115_out);
  and and_116 (and_116_out, s_r_ff_59_q, transistor_115_out);
  and and_117 (and_117_out, s_r_ff_51_q, transistor_115_out);
  and and_118 (and_118_out, s_r_ff_43_q, transistor_115_out);
  and and_119 (and_119_out, s_r_ff_35_q, transistor_115_out);
  and and_120 (and_120_out, s_r_ff_27_q, transistor_115_out);
  and and_121 (and_121_out, s_r_ff_19_q, transistor_115_out);
  and and_122 (and_122_out, s_r_ff_77_q, transistor_117_out);
  and and_123 (and_123_out, s_r_ff_69_q, transistor_117_out);
  and and_124 (and_124_out, s_r_ff_61_q, transistor_117_out);
  and and_125 (and_125_out, s_r_ff_53_q, transistor_117_out);
  and and_126 (and_126_out, s_r_ff_45_q, transistor_117_out);
  and and_127 (and_127_out, s_r_ff_37_q, transistor_117_out);
  and and_128 (and_128_out, s_r_ff_29_q, transistor_117_out);
  and and_129 (and_129_out, s_r_ff_21_q, transistor_117_out);
  and and_130 (and_130_out, s_r_ff_78_q, transistor_118_out);
  and and_131 (and_131_out, s_r_ff_70_q, transistor_118_out);
  and and_132 (and_132_out, s_r_ff_62_q, transistor_118_out);
  and and_133 (and_133_out, s_r_ff_54_q, transistor_118_out);
  and and_134 (and_134_out, s_r_ff_46_q, transistor_118_out);
  and and_135 (and_135_out, s_r_ff_38_q, transistor_118_out);
  and and_136 (and_136_out, s_r_ff_30_q, transistor_118_out);
  and and_137 (and_137_out, s_r_ff_22_q, transistor_118_out);
  and and_138 (and_138_out, s_r_ff_79_q, transistor_119_out);
  and and_139 (and_139_out, s_r_ff_71_q, transistor_119_out);
  and and_140 (and_140_out, s_r_ff_63_q, transistor_119_out);
  and and_141 (and_141_out, s_r_ff_55_q, transistor_119_out);
  and and_142 (and_142_out, s_r_ff_47_q, transistor_119_out);
  and and_143 (and_143_out, s_r_ff_39_q, transistor_119_out);
  and and_144 (and_144_out, s_r_ff_31_q, transistor_119_out);
  and and_145 (and_145_out, s_r_ff_23_q, transistor_119_out);
  and and_146 (and_146_out, s_r_ff_74_q, transistor_114_out);
  and and_147 (and_147_out, s_r_ff_66_q, transistor_114_out);
  and and_148 (and_148_out, s_r_ff_58_q, transistor_114_out);
  and and_149 (and_149_out, s_r_ff_50_q, transistor_114_out);
  and and_150 (and_150_out, s_r_ff_42_q, transistor_114_out);
  and and_151 (and_151_out, s_r_ff_34_q, transistor_114_out);
  and and_152 (and_152_out, s_r_ff_26_q, transistor_114_out);
  and and_153 (and_153_out, s_r_ff_18_q, transistor_114_out);
  and and_154 (and_154_out, s_r_ff_76_q, transistor_116_out);
  and and_155 (and_155_out, s_r_ff_68_q, transistor_116_out);
  and and_156 (and_156_out, s_r_ff_60_q, transistor_116_out);
  and and_157 (and_157_out, s_r_ff_52_q, transistor_116_out);
  and and_158 (and_158_out, s_r_ff_44_q, transistor_116_out);
  and and_159 (and_159_out, s_r_ff_36_q, transistor_116_out);
  and and_160 (and_160_out, s_r_ff_28_q, transistor_116_out);
  and and_161 (and_161_out, s_r_ff_20_q, transistor_116_out);
  LedBar ledbar_7 (
    .led0(s_r_ff_17_q), .led1(s_r_ff_25_q), .led2(s_r_ff_33_q), .led3(s_r_ff_41_q), .led4(s_r_ff_49_q),
    .led5(s_r_ff_57_q), .led6(s_r_ff_65_q), .led7(s_r_ff_73_q));
  LedBar ledbar_8 (
    .led0(s_r_ff_18_q), .led1(s_r_ff_26_q), .led2(s_r_ff_34_q), .led3(s_r_ff_42_q), .led4(s_r_ff_50_q),
    .led5(s_r_ff_58_q), .led6(s_r_ff_66_q), .led7(s_r_ff_74_q));
  LedBar ledbar_9 (
    .led0(s_r_ff_19_q), .led1(s_r_ff_27_q), .led2(s_r_ff_35_q), .led3(s_r_ff_43_q), .led4(s_r_ff_51_q),
    .led5(s_r_ff_59_q), .led6(s_r_ff_67_q), .led7(s_r_ff_75_q));
  LedBar ledbar_10 (
    .led0(s_r_ff_20_q), .led1(s_r_ff_28_q), .led2(s_r_ff_36_q), .led3(s_r_ff_44_q), .led4(s_r_ff_52_q),
    .led5(s_r_ff_60_q), .led6(s_r_ff_68_q), .led7(s_r_ff_76_q));
  LedBar ledbar_11 (
    .led0(s_r_ff_21_q), .led1(s_r_ff_29_q), .led2(s_r_ff_37_q), .led3(s_r_ff_45_q), .led4(s_r_ff_53_q),
    .led5(s_r_ff_61_q), .led6(s_r_ff_69_q), .led7(s_r_ff_77_q));
  LedBar ledbar_12 (
    .led0(s_r_ff_22_q), .led1(s_r_ff_30_q), .led2(s_r_ff_38_q), .led3(s_r_ff_46_q), .led4(s_r_ff_54_q),
    .led5(s_r_ff_62_q), .led6(s_r_ff_70_q), .led7(s_r_ff_78_q));
  LedBar ledbar_13 (
    .led0(s_r_ff_23_q), .led1(s_r_ff_31_q), .led2(s_r_ff_39_q), .led3(s_r_ff_47_q), .led4(s_r_ff_55_q),
    .led5(s_r_ff_63_q), .led6(s_r_ff_71_q), .led7(s_r_ff_79_q));
  LedBar ledbar_14 (
    .led0(s_r_ff_24_q), .led1(s_r_ff_32_q), .led2(s_r_ff_40_q), .led3(s_r_ff_48_q), .led4(s_r_ff_56_q),
    .led5(s_r_ff_64_q), .led6(s_r_ff_72_q), .led7(s_r_ff_80_q));
  and and_162 (and_162_out, buffer_81_out, transistor_120_out);
  and and_163 (and_163_out, transistor_120_out, transistor_124_out);
  and and_164 (and_164_out, buffer_97_out, transistor_127_out);
  and and_165 (and_165_out, transistor_127_out, transistor_126_out);
  and and_166 (and_166_out, buffer_113_out, transistor_130_out);
  and and_167 (and_167_out, transistor_130_out, transistor_129_out);
  and and_168 (and_168_out, buffer_129_out, transistor_132_out);
  and and_169 (and_169_out, transistor_132_out, transistor_131_out);
  and and_170 (and_170_out, buffer_145_out, transistor_133_out);
  and and_171 (and_171_out, transistor_133_out, transistor_140_out);
  and and_172 (and_172_out, buffer_161_out, transistor_121_out);
  and and_173 (and_173_out, transistor_121_out, transistor_134_out);
  and and_174 (and_174_out, buffer_177_out, transistor_136_out);
  and and_175 (and_175_out, transistor_136_out, transistor_142_out);
  and and_176 (and_176_out, buffer_193_out, transistor_123_out);
  and and_177 (and_177_out, transistor_123_out, transistor_122_out);
  S_R_Flip_Flop s_r_ff_17 (.Q(s_r_ff_17_q), .reset(and_163_out), .preset(and_162_out));  // open: S, R, clk, Qn
  S_R_Flip_Flop s_r_ff_18 (.Q(s_r_ff_18_q), .reset(and_165_out), .preset(and_164_out));  // open: S, R, clk, Qn
  S_R_Flip_Flop s_r_ff_19 (.Q(s_r_ff_19_q), .reset(and_167_out), .preset(and_166_out));  // open: S, R, clk, Qn
  S_R_Flip_Flop s_r_ff_20 (.Q(s_r_ff_20_q), .reset(and_169_out), .preset(and_168_out));  // open: S, R, clk, Qn
  S_R_Flip_Flop s_r_ff_21 (.Q(s_r_ff_21_q), .reset(and_171_out), .preset(and_170_out));  // open: S, R, clk, Qn
  S_R_Flip_Flop s_r_ff_22 (.Q(s_r_ff_22_q), .reset(and_173_out), .preset(and_172_out));  // open: S, R, clk, Qn
  S_R_Flip_Flop s_r_ff_23 (.Q(s_r_ff_23_q), .reset(and_175_out), .preset(and_174_out));  // open: S, R, clk, Qn
  S_R_Flip_Flop s_r_ff_24 (.Q(s_r_ff_24_q), .reset(and_177_out), .preset(and_176_out));  // open: S, R, clk, Qn
  and and_178 (and_178_out, buffer_80_out, transistor_120_out);
  and and_179 (and_179_out, transistor_120_out, transistor_124_out);
  and and_180 (and_180_out, buffer_96_out, transistor_127_out);
  and and_181 (and_181_out, transistor_127_out, transistor_126_out);
  and and_182 (and_182_out, buffer_112_out, transistor_130_out);
  and and_183 (and_183_out, transistor_130_out, transistor_129_out);
  and and_184 (and_184_out, buffer_128_out, transistor_132_out);
  and and_185 (and_185_out, transistor_132_out, transistor_131_out);
  and and_186 (and_186_out, buffer_144_out, transistor_133_out);
  and and_187 (and_187_out, transistor_133_out, transistor_140_out);
  and and_188 (and_188_out, buffer_160_out, transistor_121_out);
  and and_189 (and_189_out, transistor_121_out, transistor_134_out);
  and and_190 (and_190_out, buffer_176_out, transistor_136_out);
  and and_191 (and_191_out, transistor_136_out, transistor_142_out);
  and and_192 (and_192_out, buffer_192_out, transistor_123_out);
  and and_193 (and_193_out, transistor_123_out, transistor_122_out);
  S_R_Flip_Flop s_r_ff_25 (.Q(s_r_ff_25_q), .reset(and_179_out), .preset(and_178_out));  // open: S, R, clk, Qn
  S_R_Flip_Flop s_r_ff_26 (.Q(s_r_ff_26_q), .reset(and_181_out), .preset(and_180_out));  // open: S, R, clk, Qn
  S_R_Flip_Flop s_r_ff_27 (.Q(s_r_ff_27_q), .reset(and_183_out), .preset(and_182_out));  // open: S, R, clk, Qn
  S_R_Flip_Flop s_r_ff_28 (.Q(s_r_ff_28_q), .reset(and_185_out), .preset(and_184_out));  // open: S, R, clk, Qn
  S_R_Flip_Flop s_r_ff_29 (.Q(s_r_ff_29_q), .reset(and_187_out), .preset(and_186_out));  // open: S, R, clk, Qn
  S_R_Flip_Flop s_r_ff_30 (.Q(s_r_ff_30_q), .reset(and_189_out), .preset(and_188_out));  // open: S, R, clk, Qn
  S_R_Flip_Flop s_r_ff_31 (.Q(s_r_ff_31_q), .reset(and_191_out), .preset(and_190_out));  // open: S, R, clk, Qn
  S_R_Flip_Flop s_r_ff_32 (.Q(s_r_ff_32_q), .reset(and_193_out), .preset(and_192_out));  // open: S, R, clk, Qn
  and and_194 (and_194_out, buffer_79_out, transistor_120_out);
  and and_195 (and_195_out, transistor_120_out, transistor_124_out);
  and and_196 (and_196_out, buffer_95_out, transistor_127_out);
  and and_197 (and_197_out, transistor_127_out, transistor_126_out);
  and and_198 (and_198_out, buffer_111_out, transistor_130_out);
  and and_199 (and_199_out, transistor_130_out, transistor_129_out);
  and and_200 (and_200_out, buffer_127_out, transistor_132_out);
  and and_201 (and_201_out, transistor_132_out, transistor_131_out);
  and and_202 (and_202_out, buffer_143_out, transistor_133_out);
  and and_203 (and_203_out, transistor_133_out, transistor_140_out);
  and and_204 (and_204_out, buffer_159_out, transistor_121_out);
  and and_205 (and_205_out, transistor_121_out, transistor_134_out);
  and and_206 (and_206_out, buffer_175_out, transistor_136_out);
  and and_207 (and_207_out, transistor_136_out, transistor_142_out);
  and and_208 (and_208_out, buffer_191_out, transistor_123_out);
  and and_209 (and_209_out, transistor_123_out, transistor_122_out);
  S_R_Flip_Flop s_r_ff_33 (.Q(s_r_ff_33_q), .reset(and_195_out), .preset(and_194_out));  // open: S, R, clk, Qn
  S_R_Flip_Flop s_r_ff_34 (.Q(s_r_ff_34_q), .reset(and_197_out), .preset(and_196_out));  // open: S, R, clk, Qn
  S_R_Flip_Flop s_r_ff_35 (.Q(s_r_ff_35_q), .reset(and_199_out), .preset(and_198_out));  // open: S, R, clk, Qn
  S_R_Flip_Flop s_r_ff_36 (.Q(s_r_ff_36_q), .reset(and_201_out), .preset(and_200_out));  // open: S, R, clk, Qn
  S_R_Flip_Flop s_r_ff_37 (.Q(s_r_ff_37_q), .reset(and_203_out), .preset(and_202_out));  // open: S, R, clk, Qn
  S_R_Flip_Flop s_r_ff_38 (.Q(s_r_ff_38_q), .reset(and_205_out), .preset(and_204_out));  // open: S, R, clk, Qn
  S_R_Flip_Flop s_r_ff_39 (.Q(s_r_ff_39_q), .reset(and_207_out), .preset(and_206_out));  // open: S, R, clk, Qn
  S_R_Flip_Flop s_r_ff_40 (.Q(s_r_ff_40_q), .reset(and_209_out), .preset(and_208_out));  // open: S, R, clk, Qn
  and and_210 (and_210_out, buffer_78_out, transistor_120_out);
  and and_211 (and_211_out, transistor_120_out, transistor_124_out);
  and and_212 (and_212_out, buffer_94_out, transistor_127_out);
  and and_213 (and_213_out, transistor_127_out, transistor_126_out);
  and and_214 (and_214_out, buffer_110_out, transistor_130_out);
  and and_215 (and_215_out, transistor_130_out, transistor_129_out);
  and and_216 (and_216_out, buffer_126_out, transistor_132_out);
  and and_217 (and_217_out, transistor_132_out, transistor_131_out);
  and and_218 (and_218_out, buffer_142_out, transistor_133_out);
  and and_219 (and_219_out, transistor_133_out, transistor_140_out);
  and and_220 (and_220_out, buffer_158_out, transistor_121_out);
  and and_221 (and_221_out, transistor_121_out, transistor_134_out);
  and and_222 (and_222_out, buffer_174_out, transistor_136_out);
  and and_223 (and_223_out, transistor_136_out, transistor_142_out);
  and and_224 (and_224_out, buffer_190_out, transistor_123_out);
  and and_225 (and_225_out, transistor_123_out, transistor_122_out);
  S_R_Flip_Flop s_r_ff_41 (.Q(s_r_ff_41_q), .reset(and_211_out), .preset(and_210_out));  // open: S, R, clk, Qn
  S_R_Flip_Flop s_r_ff_42 (.Q(s_r_ff_42_q), .reset(and_213_out), .preset(and_212_out));  // open: S, R, clk, Qn
  S_R_Flip_Flop s_r_ff_43 (.Q(s_r_ff_43_q), .reset(and_215_out), .preset(and_214_out));  // open: S, R, clk, Qn
  S_R_Flip_Flop s_r_ff_44 (.Q(s_r_ff_44_q), .reset(and_217_out), .preset(and_216_out));  // open: S, R, clk, Qn
  S_R_Flip_Flop s_r_ff_45 (.Q(s_r_ff_45_q), .reset(and_219_out), .preset(and_218_out));  // open: S, R, clk, Qn
  S_R_Flip_Flop s_r_ff_46 (.Q(s_r_ff_46_q), .reset(and_221_out), .preset(and_220_out));  // open: S, R, clk, Qn
  S_R_Flip_Flop s_r_ff_47 (.Q(s_r_ff_47_q), .reset(and_223_out), .preset(and_222_out));  // open: S, R, clk, Qn
  S_R_Flip_Flop s_r_ff_48 (.Q(s_r_ff_48_q), .reset(and_225_out), .preset(and_224_out));  // open: S, R, clk, Qn
  and and_226 (and_226_out, buffer_77_out, transistor_120_out);
  and and_227 (and_227_out, transistor_120_out, transistor_124_out);
  and and_228 (and_228_out, buffer_93_out, transistor_127_out);
  and and_229 (and_229_out, transistor_127_out, transistor_126_out);
  and and_230 (and_230_out, buffer_109_out, transistor_130_out);
  and and_231 (and_231_out, transistor_130_out, transistor_129_out);
  and and_232 (and_232_out, buffer_125_out, transistor_132_out);
  and and_233 (and_233_out, transistor_132_out, transistor_131_out);
  and and_234 (and_234_out, buffer_141_out, transistor_133_out);
  and and_235 (and_235_out, transistor_133_out, transistor_140_out);
  and and_236 (and_236_out, buffer_157_out, transistor_121_out);
  and and_237 (and_237_out, transistor_121_out, transistor_134_out);
  and and_238 (and_238_out, buffer_173_out, transistor_136_out);
  and and_239 (and_239_out, transistor_136_out, transistor_142_out);
  and and_240 (and_240_out, buffer_189_out, transistor_123_out);
  and and_241 (and_241_out, transistor_123_out, transistor_122_out);
  S_R_Flip_Flop s_r_ff_49 (.Q(s_r_ff_49_q), .reset(and_227_out), .preset(and_226_out));  // open: S, R, clk, Qn
  S_R_Flip_Flop s_r_ff_50 (.Q(s_r_ff_50_q), .reset(and_229_out), .preset(and_228_out));  // open: S, R, clk, Qn
  S_R_Flip_Flop s_r_ff_51 (.Q(s_r_ff_51_q), .reset(and_231_out), .preset(and_230_out));  // open: S, R, clk, Qn
  S_R_Flip_Flop s_r_ff_52 (.Q(s_r_ff_52_q), .reset(and_233_out), .preset(and_232_out));  // open: S, R, clk, Qn
  S_R_Flip_Flop s_r_ff_53 (.Q(s_r_ff_53_q), .reset(and_235_out), .preset(and_234_out));  // open: S, R, clk, Qn
  S_R_Flip_Flop s_r_ff_54 (.Q(s_r_ff_54_q), .reset(and_237_out), .preset(and_236_out));  // open: S, R, clk, Qn
  S_R_Flip_Flop s_r_ff_55 (.Q(s_r_ff_55_q), .reset(and_239_out), .preset(and_238_out));  // open: S, R, clk, Qn
  S_R_Flip_Flop s_r_ff_56 (.Q(s_r_ff_56_q), .reset(and_241_out), .preset(and_240_out));  // open: S, R, clk, Qn
  and and_242 (and_242_out, buffer_76_out, transistor_120_out);
  and and_243 (and_243_out, transistor_120_out, transistor_124_out);
  and and_244 (and_244_out, buffer_92_out, transistor_127_out);
  and and_245 (and_245_out, transistor_127_out, transistor_126_out);
  and and_246 (and_246_out, buffer_108_out, transistor_130_out);
  and and_247 (and_247_out, transistor_130_out, transistor_129_out);
  and and_248 (and_248_out, buffer_124_out, transistor_132_out);
  and and_249 (and_249_out, transistor_132_out, transistor_131_out);
  and and_250 (and_250_out, buffer_140_out, transistor_133_out);
  and and_251 (and_251_out, transistor_133_out, transistor_140_out);
  and and_252 (and_252_out, buffer_156_out, transistor_121_out);
  and and_253 (and_253_out, transistor_121_out, transistor_134_out);
  and and_254 (and_254_out, buffer_172_out, transistor_136_out);
  and and_255 (and_255_out, transistor_136_out, transistor_142_out);
  and and_256 (and_256_out, buffer_188_out, transistor_123_out);
  and and_257 (and_257_out, transistor_123_out, transistor_122_out);
  S_R_Flip_Flop s_r_ff_57 (.Q(s_r_ff_57_q), .reset(and_243_out), .preset(and_242_out));  // open: S, R, clk, Qn
  S_R_Flip_Flop s_r_ff_58 (.Q(s_r_ff_58_q), .reset(and_245_out), .preset(and_244_out));  // open: S, R, clk, Qn
  S_R_Flip_Flop s_r_ff_59 (.Q(s_r_ff_59_q), .reset(and_247_out), .preset(and_246_out));  // open: S, R, clk, Qn
  S_R_Flip_Flop s_r_ff_60 (.Q(s_r_ff_60_q), .reset(and_249_out), .preset(and_248_out));  // open: S, R, clk, Qn
  S_R_Flip_Flop s_r_ff_61 (.Q(s_r_ff_61_q), .reset(and_251_out), .preset(and_250_out));  // open: S, R, clk, Qn
  S_R_Flip_Flop s_r_ff_62 (.Q(s_r_ff_62_q), .reset(and_253_out), .preset(and_252_out));  // open: S, R, clk, Qn
  S_R_Flip_Flop s_r_ff_63 (.Q(s_r_ff_63_q), .reset(and_255_out), .preset(and_254_out));  // open: S, R, clk, Qn
  S_R_Flip_Flop s_r_ff_64 (.Q(s_r_ff_64_q), .reset(and_257_out), .preset(and_256_out));  // open: S, R, clk, Qn
  and and_258 (and_258_out, buffer_75_out, transistor_120_out);
  and and_259 (and_259_out, transistor_120_out, transistor_124_out);
  and and_260 (and_260_out, buffer_91_out, transistor_127_out);
  and and_261 (and_261_out, transistor_127_out, transistor_126_out);
  and and_262 (and_262_out, buffer_107_out, transistor_130_out);
  and and_263 (and_263_out, transistor_130_out, transistor_129_out);
  and and_264 (and_264_out, buffer_123_out, transistor_132_out);
  and and_265 (and_265_out, transistor_132_out, transistor_131_out);
  and and_266 (and_266_out, buffer_139_out, transistor_133_out);
  and and_267 (and_267_out, transistor_133_out, transistor_140_out);
  and and_268 (and_268_out, buffer_155_out, transistor_121_out);
  and and_269 (and_269_out, transistor_121_out, transistor_134_out);
  and and_270 (and_270_out, buffer_171_out, transistor_136_out);
  and and_271 (and_271_out, transistor_136_out, transistor_142_out);
  and and_272 (and_272_out, buffer_187_out, transistor_123_out);
  and and_273 (and_273_out, transistor_123_out, transistor_122_out);
  S_R_Flip_Flop s_r_ff_65 (.Q(s_r_ff_65_q), .reset(and_259_out), .preset(and_258_out));  // open: S, R, clk, Qn
  S_R_Flip_Flop s_r_ff_66 (.Q(s_r_ff_66_q), .reset(and_261_out), .preset(and_260_out));  // open: S, R, clk, Qn
  S_R_Flip_Flop s_r_ff_67 (.Q(s_r_ff_67_q), .reset(and_263_out), .preset(and_262_out));  // open: S, R, clk, Qn
  S_R_Flip_Flop s_r_ff_68 (.Q(s_r_ff_68_q), .reset(and_265_out), .preset(and_264_out));  // open: S, R, clk, Qn
  S_R_Flip_Flop s_r_ff_69 (.Q(s_r_ff_69_q), .reset(and_267_out), .preset(and_266_out));  // open: S, R, clk, Qn
  S_R_Flip_Flop s_r_ff_70 (.Q(s_r_ff_70_q), .reset(and_269_out), .preset(and_268_out));  // open: S, R, clk, Qn
  S_R_Flip_Flop s_r_ff_71 (.Q(s_r_ff_71_q), .reset(and_271_out), .preset(and_270_out));  // open: S, R, clk, Qn
  S_R_Flip_Flop s_r_ff_72 (.Q(s_r_ff_72_q), .reset(and_273_out), .preset(and_272_out));  // open: S, R, clk, Qn
  and and_274 (and_274_out, buffer_74_out, transistor_120_out);
  and and_275 (and_275_out, transistor_120_out, transistor_124_out);
  and and_276 (and_276_out, buffer_90_out, transistor_127_out);
  and and_277 (and_277_out, transistor_127_out, transistor_126_out);
  and and_278 (and_278_out, buffer_106_out, transistor_130_out);
  and and_279 (and_279_out, transistor_130_out, transistor_129_out);
  and and_280 (and_280_out, buffer_122_out, transistor_132_out);
  and and_281 (and_281_out, transistor_132_out, transistor_131_out);
  and and_282 (and_282_out, buffer_138_out, transistor_133_out);
  and and_283 (and_283_out, transistor_133_out, transistor_140_out);
  and and_284 (and_284_out, buffer_154_out, transistor_121_out);
  and and_285 (and_285_out, transistor_121_out, transistor_134_out);
  and and_286 (and_286_out, buffer_170_out, transistor_136_out);
  and and_287 (and_287_out, transistor_136_out, transistor_142_out);
  and and_288 (and_288_out, buffer_186_out, transistor_123_out);
  and and_289 (and_289_out, transistor_123_out, transistor_122_out);
  S_R_Flip_Flop s_r_ff_73 (.Q(s_r_ff_73_q), .reset(and_275_out), .preset(and_274_out));  // open: S, R, clk, Qn
  S_R_Flip_Flop s_r_ff_74 (.Q(s_r_ff_74_q), .reset(and_277_out), .preset(and_276_out));  // open: S, R, clk, Qn
  S_R_Flip_Flop s_r_ff_75 (.Q(s_r_ff_75_q), .reset(and_279_out), .preset(and_278_out));  // open: S, R, clk, Qn
  S_R_Flip_Flop s_r_ff_76 (.Q(s_r_ff_76_q), .reset(and_281_out), .preset(and_280_out));  // open: S, R, clk, Qn
  S_R_Flip_Flop s_r_ff_77 (.Q(s_r_ff_77_q), .reset(and_283_out), .preset(and_282_out));  // open: S, R, clk, Qn
  S_R_Flip_Flop s_r_ff_78 (.Q(s_r_ff_78_q), .reset(and_285_out), .preset(and_284_out));  // open: S, R, clk, Qn
  S_R_Flip_Flop s_r_ff_79 (.Q(s_r_ff_79_q), .reset(and_287_out), .preset(and_286_out));  // open: S, R, clk, Qn
  S_R_Flip_Flop s_r_ff_80 (.Q(s_r_ff_80_q), .reset(and_289_out), .preset(and_288_out));  // open: S, R, clk, Qn
  Transistor transistor_112 (.in(button_6_out), .out(transistor_112_out), .gate(1'b0));
  Button button_6 (.out(button_6_out));
  Transistor transistor_113 (.in(button_7_out), .out(transistor_113_out), .gate(1'b0));
  DipSwitch dipswitch_6 (.sw1(dipswitch_6_sw1), .sw4(dipswitch_6_sw4));  // open: sw2, sw3, sw5, sw6, sw7, sw8
  Button button_7 (.out(button_7_out));
  Transistor transistor_114 (.in(button_8_out), .out(transistor_114_out), .gate(1'b0));
  Button button_8 (.out(button_8_out));
  Transistor transistor_115 (.in(button_9_out), .out(transistor_115_out), .gate(1'b0));
  Button button_9 (.out(button_9_out));
  Transistor transistor_116 (.in(button_10_out), .out(transistor_116_out), .gate(1'b0));
  Button button_10 (.out(button_10_out));
  Transistor transistor_117 (.in(button_11_out), .out(transistor_117_out), .gate(1'b0));
  Button button_11 (.out(button_11_out));
  Transistor transistor_118 (.in(button_12_out), .out(transistor_118_out), .gate(1'b0));
  DipSwitch dipswitch_7 (.sw4(dipswitch_7_sw4));  // open: sw1, sw2, sw3, sw5, sw6, sw7, sw8
  Button button_12 (.out(button_12_out));
  Transistor transistor_119 (.in(button_13_out), .out(transistor_119_out), .gate(1'b0));
  Button button_13 (.out(button_13_out));
  DipSwitch dipswitch_8 (.sw4(dipswitch_8_sw4));  // open: sw1, sw2, sw3, sw5, sw6, sw7, sw8
  Transistor transistor_120 (.in(dipswitch_6_sw4), .out(transistor_120_out), .gate(1'b0));
  DipSwitch dipswitch_9 (.sw4(dipswitch_9_sw4));  // open: sw1, sw2, sw3, sw5, sw6, sw7, sw8
  DipSwitch dipswitch_10 (.sw4(dipswitch_10_sw4));  // open: sw1, sw2, sw3, sw5, sw6, sw7, sw8
  DipSwitch dipswitch_11 (.sw4(dipswitch_11_sw4));  // open: sw1, sw2, sw3, sw5, sw6, sw7, sw8
  DipSwitch dipswitch_12 (.sw4(dipswitch_12_sw4));  // open: sw1, sw2, sw3, sw5, sw6, sw7, sw8
  Transistor transistor_121 (.in(dipswitch_7_sw4), .out(transistor_121_out), .gate(1'b0));
  DipSwitch dipswitch_13 (.sw4(dipswitch_13_sw4));  // open: sw1, sw2, sw3, sw5, sw6, sw7, sw8
  Transistor transistor_122 (.in(dipswitch_14_sw1), .out(transistor_122_out), .gate(1'b0));
  Transistor transistor_123 (.in(dipswitch_8_sw4), .out(transistor_123_out), .gate(1'b0));
  Transistor transistor_124 (.in(dipswitch_14_sw1), .out(transistor_124_out), .gate(1'b0));
  Transistor transistor_125 (.in(button_14_out), .out(transistor_124_out), .gate(1'b0));
  Button button_14 (.out(button_14_out));
  Transistor transistor_126 (.in(dipswitch_14_sw1), .out(transistor_126_out), .gate(1'b0));
  Transistor transistor_127 (.in(dipswitch_9_sw4), .out(transistor_127_out), .gate(1'b0));
  Transistor transistor_128 (.in(button_15_out), .out(transistor_126_out), .gate(1'b0));
  Button button_15 (.out(button_15_out));
  Transistor transistor_129 (.in(dipswitch_14_sw1), .out(transistor_129_out), .gate(1'b0));
  Transistor transistor_130 (.in(dipswitch_10_sw4), .out(transistor_130_out), .gate(1'b0));
  Transistor transistor_131 (.in(dipswitch_14_sw1), .out(transistor_131_out), .gate(1'b0));
  Transistor transistor_132 (.in(dipswitch_11_sw4), .out(transistor_132_out), .gate(1'b0));
  Transistor transistor_133 (.in(dipswitch_12_sw4), .out(transistor_133_out), .gate(1'b0));
  Transistor transistor_134 (.in(dipswitch_14_sw1), .out(transistor_134_out), .gate(1'b0));
  Transistor transistor_135 (.in(button_16_out), .out(transistor_134_out), .gate(1'b0));
  Button button_16 (.out(button_16_out));
  Transistor transistor_136 (.in(dipswitch_13_sw4), .out(transistor_136_out), .gate(1'b0));
  Transistor transistor_137 (.in(button_17_out), .out(transistor_122_out), .gate(1'b0));
  Button button_17 (.out(button_17_out));
  Transistor transistor_138 (.in(button_18_out), .out(transistor_129_out), .gate(1'b0));
  Button button_18 (.out(button_18_out));
  Transistor transistor_139 (.in(button_19_out), .out(transistor_131_out), .gate(1'b0));
  Button button_19 (.out(button_19_out));
  Transistor transistor_140 (.in(dipswitch_14_sw1), .out(transistor_140_out), .gate(1'b0));
  Transistor transistor_141 (.in(button_20_out), .out(transistor_140_out), .gate(1'b0));
  Button button_20 (.out(button_20_out));
  Transistor transistor_142 (.in(dipswitch_14_sw1), .out(transistor_142_out), .gate(1'b0));
  Transistor transistor_143 (.in(button_21_out), .out(transistor_142_out), .gate(1'b0));
  Button button_21 (.out(button_21_out));
  Transistor transistor_144 (.in(dipswitch_14_sw8), .out(transistor_120_out), .gate(1'b0));
  Transistor transistor_145 (.in(dipswitch_14_sw8), .out(transistor_127_out), .gate(1'b0));
  Transistor transistor_146 (.in(dipswitch_14_sw8), .out(transistor_121_out), .gate(1'b0));
  Transistor transistor_147 (.in(dipswitch_14_sw8), .out(transistor_123_out), .gate(1'b0));
  Transistor transistor_148 (.in(dipswitch_14_sw8), .out(transistor_130_out), .gate(1'b0));
  Transistor transistor_149 (.in(dipswitch_14_sw8), .out(transistor_132_out), .gate(1'b0));
  Transistor transistor_150 (.in(dipswitch_14_sw8), .out(transistor_133_out), .gate(1'b0));
  Transistor transistor_151 (.in(dipswitch_14_sw8), .out(transistor_136_out), .gate(1'b0));
  DipSwitch dipswitch_14 (.sw1(dipswitch_14_sw1), .sw8(dipswitch_14_sw8));  // open: sw2, sw3, sw4, sw5, sw6, sw7
  and and_290 (and_290_out, rom_1_data[16], rom_1_data[17]);
  and and_291 (and_291_out, rom_1_data[15], rom_1_data[17]);
  and and_292 (and_292_out, rom_1_data[14], rom_1_data[17]);
  and and_293 (and_293_out, rom_1_data[13], rom_1_data[17]);
  and and_294 (and_294_out, rom_1_data[12], rom_1_data[17]);
  and and_295 (and_295_out, rom_1_data[11], rom_1_data[17]);
  and and_296 (and_296_out, rom_1_data[10], rom_1_data[17]);
  and and_297 (and_297_out, rom_1_data[9], rom_1_data[17]);
  Demultiplexer #(.select(3)) demultiplexer_1 (
    .out0(transistor_113_out), .out1(transistor_114_out), .out2(transistor_115_out),
    .out3(transistor_116_out), .out4(transistor_117_out), .out5(transistor_118_out),
    .out6(transistor_119_out), .out7(transistor_112_out), .in(rom_1_data[0]), .sel(rom_1_data_2));
  Demultiplexer #(.select(3)) demultiplexer_2 (
    .out0(transistor_120_out), .out1(transistor_127_out), .out2(transistor_130_out),
    .out3(transistor_132_out), .out4(transistor_133_out), .out5(transistor_121_out),
    .out6(transistor_136_out), .out7(transistor_123_out), .in(rom_1_data[1]), .sel(rom_1_data_2));
  Demultiplexer #(.select(3)) demultiplexer_3 (
    .out0(transistor_124_out), .out1(transistor_126_out), .out2(transistor_129_out),
    .out3(transistor_131_out), .out4(transistor_140_out), .out5(transistor_134_out),
    .out6(transistor_142_out), .out7(transistor_122_out), .in(rom_1_data[2]), .sel(rom_1_data_2));
  Demultiplexer demultiplexer_4 (
    .out0(transistor_44_out), .out1(transistor_45_out), .in(rom_1_data[6]), .sel(rom_1_data[8]));
  Demultiplexer demultiplexer_5 (
    .out0(transistor_46_out), .out1(transistor_47_out), .in(rom_1_data[7]), .sel(rom_1_data[8]));
  Transistor transistor_152 (.in(and_290_out), .out(buffer_49_out), .gate(1'b0));
  Transistor transistor_153 (.in(and_291_out), .out(buffer_48_out), .gate(1'b0));
  Transistor transistor_154 (.in(and_292_out), .out(buffer_47_out), .gate(1'b0));
  Transistor transistor_155 (.in(and_293_out), .out(buffer_46_out), .gate(1'b0));
  Transistor transistor_156 (.in(and_294_out), .out(buffer_45_out), .gate(1'b0));
  Transistor transistor_157 (.in(and_295_out), .out(buffer_44_out), .gate(1'b0));
  Transistor transistor_158 (.in(and_296_out), .out(buffer_43_out), .gate(1'b0));
  Transistor transistor_159 (.in(and_297_out), .out(buffer_42_out), .gate(1'b0));
  Transistor transistor_160 (.in(buffer_49_out), .out(transistor_160_out), .gate(1'b0));
  Transistor transistor_161 (.in(buffer_48_out), .out(transistor_161_out), .gate(1'b0));
  Transistor transistor_162 (.in(buffer_47_out), .out(transistor_162_out), .gate(1'b0));
  Transistor transistor_163 (.in(buffer_46_out), .out(transistor_163_out), .gate(1'b0));
  Transistor transistor_164 (.in(buffer_45_out), .out(transistor_164_out), .gate(1'b0));
  Transistor transistor_165 (.in(buffer_44_out), .out(transistor_165_out), .gate(1'b0));
  Transistor transistor_166 (.in(buffer_43_out), .out(transistor_166_out), .gate(1'b0));
  Transistor transistor_167 (.in(buffer_42_out), .out(transistor_167_out), .gate(1'b0));
  Transistor transistor_168 (.in(buffer_41_out), .out(transistor_168_out), .gate(1'b0));
  DipSwitch dipswitch_15 (
    .sw1(rom_1_data[9]), .sw2(rom_1_data[10]), .sw3(rom_1_data[11]), .sw4(rom_1_data[12]),
    .sw5(rom_1_data[13]), .sw6(rom_1_data[14]), .sw7(rom_1_data[15]), .sw8(rom_1_data[16]));
  ROM #(.addrWidth(24), .dataWidth(24)) rom_1 (
    .addr(undriven_54),
    .data({rom_1_data[23:6], rom_1_data_2[0], rom_1_data_2[1], rom_1_data_2[2], rom_1_data[2:0]}));
  J_K_Flip_Flop j_k_ff_9 (
    .J(1'b1), .K(1'b1), .clk(j_k_ff_10_q), .Q(j_k_ff_9_q), .reset(button_22_out));  // open: Qn, preset
  J_K_Flip_Flop j_k_ff_10 (
    .J(1'b1), .K(1'b1), .clk(j_k_ff_11_q), .Q(j_k_ff_10_q), .reset(button_22_out));  // open: Qn, preset
  J_K_Flip_Flop j_k_ff_11 (
    .J(1'b1), .K(1'b1), .clk(j_k_ff_12_q), .Q(j_k_ff_11_q), .reset(button_22_out));  // open: Qn, preset
  LED led_2 (.in(transistor_168_out));
  LedBar ledbar_15 (
    .led0(transistor_167_out), .led1(transistor_166_out), .led2(transistor_165_out),
    .led3(transistor_164_out), .led4(transistor_163_out), .led5(transistor_162_out),
    .led6(transistor_161_out), .led7(transistor_160_out));
  J_K_Flip_Flop j_k_ff_12 (
    .J(1'b1), .K(1'b1), .clk(j_k_ff_13_q), .Q(j_k_ff_12_q), .reset(button_22_out));  // open: Qn, preset
  J_K_Flip_Flop j_k_ff_13 (
    .J(1'b1), .K(1'b1), .clk(j_k_ff_14_q), .Q(j_k_ff_13_q), .reset(button_22_out));  // open: Qn, preset
  J_K_Flip_Flop j_k_ff_14 (
    .J(1'b1), .K(1'b1), .clk(j_k_ff_15_q), .Q(j_k_ff_14_q), .reset(button_22_out));  // open: Qn, preset
  J_K_Flip_Flop j_k_ff_15 (
    .J(1'b1), .K(1'b1), .clk(j_k_ff_16_q), .Q(j_k_ff_15_q), .reset(button_22_out));  // open: Qn, preset
  J_K_Flip_Flop j_k_ff_16 (
    .J(1'b1), .K(1'b1), .clk(digital_oscilloscope_2_p1), .Q(j_k_ff_16_q), .reset(button_22_out));  // open: Qn, preset
  Clock clock_2 (.out(clock_2_out));
  Button button_22 (.out(button_22_out));
  // Digital_Oscilloscope digital_oscilloscope_2: pin names not known; wires that end beside it: digital_oscilloscope_2_p1, digital_oscilloscope_2_p2
  LedBar ledbar_16 (
    .led0(not_9_out), .led1(not_10_out), .led2(not_11_out), .led3(not_12_out), .led4(not_13_out),
    .led5(not_14_out), .led6(not_15_out), .led7(digital_oscilloscope_2_p2));
  // Switch switch_2: pin names not known; wires that end beside it: 1'b1, clock_2_out, digital_oscilloscope_2_p1
  DipSwitch dipswitch_16 (.sw8(dipswitch_16_sw8));  // open: sw1, sw2, sw3, sw4, sw5, sw6, sw7
  not not_9 (not_9_out, j_k_ff_9_q);
  not not_10 (not_10_out, j_k_ff_10_q);
  not not_11 (not_11_out, j_k_ff_11_q);
  not not_12 (not_12_out, j_k_ff_12_q);
  not not_13 (not_13_out, j_k_ff_13_q);
  not not_14 (not_14_out, j_k_ff_14_q);
  not not_15 (not_15_out, j_k_ff_15_q);
  not not_16 (digital_oscilloscope_2_p2, j_k_ff_16_q);
  and and_298 (and_298_out, not_9_out, dipswitch_16_sw8);
  and and_299 (and_299_out, not_10_out, dipswitch_16_sw8);
  and and_300 (and_300_out, not_11_out, dipswitch_16_sw8);
  and and_301 (and_301_out, not_12_out, dipswitch_16_sw8);
  and and_302 (and_302_out, not_13_out, dipswitch_16_sw8);
  and and_303 (and_303_out, not_14_out, dipswitch_16_sw8);
  and and_304 (and_304_out, not_15_out, dipswitch_16_sw8);
  and and_305 (and_305_out, digital_oscilloscope_2_p2, dipswitch_16_sw8);
  ROM rom_2 (.addr(buffer_201_out), .data(rom_2_data));
  LedBar ledbar_17 (
    .led0(rom_2_data[7]), .led1(rom_2_data[6]), .led2(rom_2_data[5]), .led3(rom_2_data[4]),
    .led4(rom_2_data[3]), .led5(rom_2_data[2]), .led6(rom_2_data[1]), .led7(rom_2_data[0]));
  buf buffer_194 (buffer_201_out[7], and_298_out);
  buf buffer_195 (buffer_201_out[6], and_299_out);
  buf buffer_196 (buffer_201_out[5], and_300_out);
  buf buffer_197 (buffer_201_out[4], and_301_out);
  buf buffer_198 (buffer_201_out[3], and_302_out);
  buf buffer_199 (buffer_201_out[2], and_303_out);
  buf buffer_200 (buffer_201_out[1], and_304_out);
  buf buffer_201 (buffer_201_out[0], and_305_out);
  ROM rom_3 (.addr(dipswitch_17_sw8), .data(rom_3_data));
  DipSwitch dipswitch_17 (
    .sw1(dipswitch_17_sw8[7]), .sw2(dipswitch_17_sw8[6]), .sw3(dipswitch_17_sw8[5]),
    .sw4(dipswitch_17_sw8[4]), .sw5(dipswitch_17_sw8[3]), .sw6(dipswitch_17_sw8[2]),
    .sw7(dipswitch_17_sw8[1]), .sw8(dipswitch_17_sw8[0]));
  LedBar ledbar_18 (
    .led0(rom_3_data[7]), .led1(rom_3_data[6]), .led2(rom_3_data[5]), .led3(rom_3_data[4]),
    .led4(rom_3_data[3]), .led5(rom_3_data[2]), .led6(rom_3_data[1]), .led7(rom_3_data[0]));
  Button button_23 (.out(button_23_out));
  and and_306 (and_306_out, button_23_out, 1'b0);
  LED led_3 (.in(and_306_out));

  // Notes on the sheet:
  //   A
  //   B
  //   Sum
  //   A
  //   Carry OUT
  //   Carry IN
  //   Sum
  //   B
  //   Carry IN
  //   A
  //   B
  //   Carry OUT
  //   Sum
  //   Carry OUT
  //   Carry IN
  //   A
  //   Sum
  //   B
  //   Carry IN
  //   Carry OUT
  //   B
  //   A
  //   Sum
  //   Carry IN
  //   Carry OUT
  //   A
  //   B
  //   Sum
  //   Carry IN
  //   Carry OUT
  //   A
  //   Sum
  //   B
  //   Carry IN
  //   8 bit Buffer - A
  //   8 bit Buffer - B
  //   Carry OUT
  //   A
  //   B
  //   Sum
  //   Carry IN
  //   Carry OUT
  //   Sum
  //   Carry
  //   S
  //   E
  //   R
  //   S
  //   E
  //   R
  //   Q
  //   Q
  //   ->
  //   ->
  //   ->
  //   ->
  //   ->
  //   ->
  //   ->
  //   ->
  //   ->
  //   Carry
  //   A
  //   B7
  //   B
  //   Carry IN
  //   S
  //   E
  //   R
  //   S
  //   E
  //   R
  //   A
  //   B
  //   ->
  //   ->
  //   ->
  //   ->
  //   ->
  //   ->
  //   ->
  //   ->
  //   Carry IN
  //   Q
  //   B6
  //   Q
  //   S
  //   E
  //   R
  //   S
  //   E
  //   R
  //   A
  //   B
  //   Q
  //   Carry IN
  //   B5
  //   Q
  //   S
  //   E
  //   R
  //   A
  //   S
  //   E
  //   R
  //   B
  //   Carry IN
  //   Q
  //   B4
  //   Q
  //   A
  //   S
  //   E
  //   R
  //   S
  //   Arithematic Unit
  //   B
  //   E
  //   R
  //   Carry IN
  //   Q
  //   Q
  //   B3
  //   A
  //   B
  //   S
  //   E
  //   R
  //   S
  //   E
  //   R
  //   Carry IN
  //   8 bit Binary Counter
  //   A
  //   Q
  //   B2
  //   Q
  //   B
  //   S
  //   Carry IN
  //   E
  //   R
  //   S
  //   E
  //   R
  //   A
  //   Q
  //   B
  //   B1
  //   Q
  //   S
  //   E
  //   R
  //   Secondary Address Bus Control Unit
  //   Carry IN
  //   S
  //   E
  //   R
  //   K
  //   Q
  //   B0
  //   Q
  //   OUTPUT ENABLE
  //   ->
  //   ->
  //   ->
  //   ->
  //   ->
  //   ->
  //   ->
  //   ->
  //   ->
  //   ->
  //   ->
  //   ->
  //   ->
  //   OUTPUT ENABLE
  //   ->
  //   ->
  //   ->
  //   ->
  //   ->
  //   ->
  //   ->
  //   ->
  //   ->
  //   ->
  //   ->
  //   ->
  //   ->
  //   ->
  //   RESET
  //   ENABLE
  //   RESET
  //   ENABLE
  //   ->
  //   ->
  //   A0
  //   A0
  //   A1
  //   A1
  //   A2
  //   A2
  //   A3
  //   A3
  //   Data Bus
  //   A4
  //   A4
  //   A5
  //   A5
  //   A6
  //   A6
  //   A7
  //   A7
  //   A8 (Carry Bit)
  //   A8 (Carry Bit)
  //   A9
  //   A10
  //   A10
  //   A11
  //   A11
  //   A12
  //   A13
  //   A12
  //   A13
  //   A14
  //   A14
  //   A15
  //   A15
  //   A16
  //   A16
  //   ->
  //   ->
  //   ->
  //   ->
  //   ->
  //   ->
  //   ->
  //   ->
  //   ->
  //   ->
  //   ->
  //   ->
  //   ->
  //   ->
  //   ->
  //   ->
  //   ->
  //   ->
  //   ->
  //   ->
  //   ->
  //   ->
  //   ->
  //   ->
  //   ->
  //   ->
  //   ->
  //   ->
  //   ->
  //   ->
  //   ->
  //   ->
  //   ->
  //   ->
  //   ->
  //   ->
  //   ->
  //   ->
  //   ->
  //   ->
  //   ->
  //   ->
  //   ->
  //   ->
  //   ->
  //   ->
  //   ->
  //   ->
  //   ->
  //   ->
  //   ->
  //   ->
  //   ->
  //   ->
  //   ->
  //   ->
  //   ->
  //   ->
  //   ->
  //   ->
  //   ->
  //   ->
  //   ->
  //   ->
  //   S
  //   E
  //   R
  //   S
  //   E
  //   R
  //   S
  //   E
  //   R
  //   S
  //   E
  //   R
  //   S
  //   E
  //   R
  //   S
  //   E
  //   R
  //   S
  //   E
  //   R
  //   S
  //   E
  //   R
  //   Q
  //   Q
  //   Q
  //   Q
  //   Q
  //   Q
  //   Q
  //   Q
  //   S
  //   E
  //   R
  //   S
  //   E
  //   R
  //   S
  //   E
  //   R
  //   S
  //   E
  //   R
  //   S
  //   E
  //   R
  //   S
  //   E
  //   R
  //   S
  //   E
  //   R
  //   S
  //   E
  //   R
  //   Q
  //   Q
  //   Q
  //   Q
  //   Q
  //   Q
  //   Q
  //   Q
  //   S
  //   E
  //   R
  //   S
  //   E
  //   R
  //   S
  //   E
  //   R
  //   S
  //   E
  //   R
  //   S
  //   E
  //   R
  //   S
  //   E
  //   R
  //   S
  //   E
  //   R
  //   S
  //   E
  //   R
  //   Q
  //   Q
  //   Q
  //   Q
  //   Q
  //   Q
  //   Q
  //   Q
  //   Temporary Storage Unit
  //   S
  //   E
  //   R
  //   S
  //   E
  //   R
  //   S
  //   E
  //   R
  //   S
  //   E
  //   R
  //   S
  //   E
  //   R
  //   S
  //   E
  //   R
  //   S
  //   E
  //   R
  //   S
  //   E
  //   R
  //   Q
  //   Q
  //   Q
  //   Q
  //   Q
  //   Q
  //   Q
  //   Q
  //   S
  //   E
  //   R
  //   S
  //   E
  //   R
  //   S
  //   E
  //   R
  //   S
  //   E
  //   R
  //   S
  //   E
  //   R
  //   S
  //   E
  //   R
  //   S
  //   E
  //   R
  //   S
  //   E
  //   R
  //   Q
  //   Q
  //   Q
  //   Q
  //   Q
  //   Q
  //   Q
  //   Q
  //   S
  //   E
  //   R
  //   S
  //   E
  //   R
  //   S
  //   E
  //   R
  //   S
  //   E
  //   R
  //   S
  //   E
  //   R
  //   S
  //   E
  //   R
  //   S
  //   E
  //   R
  //   S
  //   E
  //   R
  //   Q
  //   Q
  //   Q
  //   Q
  //   Q
  //   Q
  //   Q
  //   Q
  //   S
  //   E
  //   R
  //   S
  //   E
  //   R
  //   S
  //   E
  //   R
  //   S
  //   E
  //   R
  //   S
  //   E
  //   R
  //   S
  //   E
  //   R
  //   S
  //   E
  //   R
  //   S
  //   E
  //   R
  //   Q
  //   Q
  //   Q
  //   Q
  //   Q
  //   Q
  //   Q
  //   Q
  //   S
  //   E
  //   R
  //   S
  //   E
  //   R
  //   S
  //   E
  //   R
  //   S
  //   E
  //   R
  //   S
  //   E
  //   R
  //   S
  //   E
  //   R
  //   S
  //   E
  //   R
  //   S
  //   E
  //   R
  //   Q
  //   Q
  //   Q
  //   Q
  //   Q
  //   Q
  //   Q
  //   Q
  //   INPUT ENABLE
  //   OUT Enable
  //   OUT Enable
  //   OUT Enable
  //   OUT Enable
  //   OUT Enable
  //   OUT Enable
  //   OUT Enable
  //   INPUT ENABLE
  //   OUT Enable
  //   RESET
  //   INPUT ENABLE
  //   RESET
  //   RESET
  //   RESET
  //   RESET
  //   RESET
  //   IN Enable
  //   Diode
  //   ->
  //   ->
  //   IN Enable
  //   ->
  //   IN Enable
  //   IN Enable
  //   RESET
  //   Diode
  //   ->
  //   ->
  //   IN Enable
  //   Diode
  //   ->
  //   ->
  //   ->
  //   ->
  //   RESET
  //   Diode
  //   ->
  //   ->
  //   RESET
  //   Diode
  //   ->
  //   ->
  //   ->
  //   Diode
  //   ->
  //   ->
  //   IN Enable
  //   Diode
  //   ->
  //   ->
  //   IN Enable
  //   ->
  //   RESET
  //   Diode
  //   ->
  //   ->
  //   IN Enable
  //   RESET
  //   RESET
  //   ->
  //   RESET
  //   ->
  //   RESET
  //   ->
  //   RESET
  //   ->
  //   Clear All Register
  //   ->
  //   ->
  //   ->
  //   ->
  //   ->
  //   ->
  //   ->
  //   Register A
  //   Register B
  //   Register C
  //   Register D
  //   Register E
  //   Register F
  //   Register G
  //   Register H
  //   RESET
  //   Enable
  //   Control Unit
  //   IN ENABLE
  //   RESET
  //   OUT ENABLE
  //   0 -> A Buffer | 1 -> B Buffer
  //   A0, A1, A2, A3, A4, A5, A6, A7
  //   Enable
  //   RESET
  //   ->
  //   ->
  //   ->
  //   ->
  //   ->
  //   ->
  //   ->
  //   ->
  //   ->
  //   ->
  //   ->
  //   ->
  //   ->
  //   ->
  //   ->
  //   ->
  //   ->
  //   LSB
  //   HSB
  //   Storage Unit
  //   Arithematic Unit Output on Address Bus Enable
  //   Carry
  //   contents of rom_1 (hex, n*v repeats v):
  //   0 1 2 3 4 5 6 7 8 9 a b c d e f 10 11 12 13 14 15 16 17 18 19
  //   8 bit Binary Counter
  //   OUTPUT ENABLE
  //   contents of rom_2 (hex, n*v repeats v):
  //   1 2 3 4 5 6 7 8
  //   contents of rom_3 (hex, n*v repeats v):
  //   0 1 2 3 4 5 6 7 8 9 a b c d e f
endmodule
